// Logisim project RV32I_v1_Rtype_Multi_support.circ as structural Verilog: 7 circuits, main circuit main
module main (
  input  RST,
  output [6:0] out_2,
  output [4:0] out_3,
  output [2:0] out_4,
  output [4:0] out_5,
  output [6:0] out_6,
  output [31:0] out_7,
  output [4:0] out_8
);

  wire CLK, id_ex_1_regwenout, RegWEn;
  wire [3:0] ALUSel, id_ex_1_aluselout;
  wire [31:0] adder_1_out, imem_1_inst, INSTRUCTION, regfile_1_dataa, regfile_1_datab, register_1_q;

  Register #(.width(32)) register_1 (.D(adder_1_out), .clk(CLK), .Q(register_1_q), .clr(RST));  // open: en
  Adder #(.width(32)) adder_1 (.a(32'h4), .b(register_1_q), .out(adder_1_out));  // open: cin, cout
  CONTROL_LOGIC control_logic_1 (
    .Inst(INSTRUCTION), .out_2(out_2), .out_3(out_3), .out_4(out_4), .out_5(out_5), .out_6(out_8),
    .out_7(out_6), .RegWEn(RegWEn), .ALUSel(ALUSel));
  IMEM imem_1 (.ADDR(register_1_q), .INST(imem_1_inst));
  Register #(.width(32)) PCid (.D(register_1_q));  // open: en, clk, Q, clr
  Register #(.width(32)) INSTid (.D(imem_1_inst), .Q(INSTRUCTION));  // open: en, clk, clr
  RegFile regfile_1 (
    .DataD(out_7), .AddrD(INSTRUCTION[11:7]), .AddrA(INSTRUCTION[19:15]), .AddrB(INSTRUCTION[24:20]),
    .in_5(id_ex_1_regwenout), .in_6(CLK), .DataA(regfile_1_dataa), .DataB(regfile_1_datab));
  ID_EX id_ex_1 (
    .RegWEn(RegWEn), .ALUSel(ALUSel), .CLK(CLK), .RegWEnOut(id_ex_1_regwenout), .ALUSelOut(id_ex_1_aluselout));
  Clock clock_1 (.out(CLK));
  ALU alu_1 (.rs1(regfile_1_dataa), .rs2(regfile_1_datab), .OP(id_ex_1_aluselout), .R(out_7));

  // Other names for the same wires on the sheet: ALU_Out[31:0] = out_7; FUNCT3[2:0] = out_4; FUNCT7[6:0] = out_6;
  //   OPCODE[6:0] = out_2; RD[4:0] = out_3; RS1[4:0] = out_5; RS2[4:0] = out_8

  // Notes on the sheet:
  //   CONTROL LOGIC
endmodule

module IMEM (
  input  [31:0] ADDR,
  output [31:0] INST
);

  ROM #(.addrWidth(24), .dataWidth(32)) rom_1 (.addr(ADDR[25:2]), .data(INST));

  // Notes on the sheet:
  //   ROM
endmodule

module RegFile (
  input  [31:0] DataD,
  input  [4:0] AddrD,
  input  [4:0] AddrA,
  input  [4:0] AddrB,
  input  in_5,
  input  in_6,
  output [31:0] DataA,
  output [31:0] DataB
);

  wire WE_1, WE_2, WE_3, WE_4, WE_5, WE_6, WE_7, WE_8, WE_9, WE_10, WE_11, WE_12, WE_13, WE_14, WE_15, WE_16,
       WE_17, WE_18, WE_19, WE_20, WE_21, WE_22, WE_23, WE_24, WE_25, WE_26, WE_27, WE_28, WE_29, WE_30,
       WE_31;
  wire [31:0] in_r1, in_r2, in_r3, in_r4, in_r5, in_r6, in_r7, in_r8, in_r9, in_r10, in_r11, in_r12, in_r13,
       in_r14, in_r15, in_r16, in_r17, in_r18, in_r19, in_r20, in_r21, in_r22, in_r23, in_r24, in_r25,
       in_r26, in_r27, in_r28, in_r29, in_r30, in_r31, out_r1, out_r2, out_r3, out_r4, out_r5, out_r6,
       out_r7, out_r8, out_r9, out_r10, out_r11, out_r12, out_r13, out_r14, out_r15, out_r16, out_r17,
       out_r18, out_r19, out_r20, out_r21, out_r22, out_r23, out_r24, out_r25, out_r26, out_r27, out_r28,
       out_r29, out_r30, out_r31;

  Register #(.width(32)) register_1 (.D(in_r1), .en(WE_1), .clk(in_6), .Q(out_r1));  // open: clr
  Register #(.width(32)) register_2 (.D(in_r9), .en(WE_9), .clk(in_6), .Q(out_r9));  // open: clr
  Register #(.width(32)) register_3 (.D(in_r17), .en(WE_17), .clk(in_6), .Q(out_r17));  // open: clr
  Register #(.width(32)) register_4 (.D(in_r25), .en(WE_25), .clk(in_6), .Q(out_r25));  // open: clr
  Multiplexer #(.select(5), .width(32), .enable("false")) multiplexer_1 (
    .in0({32{1'b0}}), .in1(out_r1), .in2(out_r2), .in3(out_r3), .in4(out_r4), .in5(out_r5), .in6(out_r6),
    .in7(out_r7), .in8(out_r8), .in9(out_r9), .in10(out_r10), .in11(out_r11), .in12(out_r12), .in13(out_r13),
    .in14(out_r14), .in15(out_r15), .in16(out_r16), .in17(out_r17), .in18(out_r18), .in19(out_r19),
    .in20(out_r20), .in21(out_r21), .in22(out_r22), .in23(out_r23), .in24(out_r24), .in25(out_r25),
    .in26(out_r26), .in27(out_r27), .in28(out_r28), .in29(out_r29), .in30(out_r30), .in31(out_r31),
    .out(DataA), .sel(AddrA));
  Register #(.width(32)) register_5 (.D(in_r2), .en(WE_2), .clk(in_6), .Q(out_r2));  // open: clr
  Register #(.width(32)) register_6 (.D(in_r10), .en(WE_10), .clk(in_6), .Q(out_r10));  // open: clr
  Register #(.width(32)) register_7 (.D(in_r18), .en(WE_18), .clk(in_6), .Q(out_r18));  // open: clr
  Register #(.width(32)) register_8 (.D(in_r26), .en(WE_26), .clk(in_6), .Q(out_r26));  // open: clr
  Register #(.width(32)) register_9 (.D(in_r3), .en(WE_3), .clk(in_6), .Q(out_r3));  // open: clr
  Register #(.width(32)) register_10 (.D(in_r11), .en(WE_11), .clk(in_6), .Q(out_r11));  // open: clr
  Register #(.width(32)) register_11 (.D(in_r19), .en(WE_19), .clk(in_6), .Q(out_r19));  // open: clr
  Register #(.width(32)) register_12 (.D(in_r27), .en(WE_27), .clk(in_6), .Q(out_r27));  // open: clr
  Multiplexer #(.select(5), .width(32), .enable("false")) multiplexer_2 (
    .in0({32{1'b0}}), .in1(out_r1), .in2(out_r2), .in3(out_r3), .in4(out_r4), .in5(out_r5), .in6(out_r6),
    .in7(out_r7), .in8(out_r8), .in9(out_r9), .in10(out_r10), .in11(out_r11), .in12(out_r12), .in13(out_r13),
    .in14(out_r14), .in15(out_r15), .in16(out_r16), .in17(out_r17), .in18(out_r18), .in19(out_r19),
    .in20(out_r20), .in21(out_r21), .in22(out_r22), .in23(out_r23), .in24(out_r24), .in25(out_r25),
    .in26(out_r26), .in27(out_r27), .in28(out_r28), .in29(out_r29), .in30(out_r30), .in31(out_r31),
    .out(DataB), .sel(AddrB));
  Register #(.width(32)) register_13 (.D(in_r4), .en(WE_4), .clk(in_6), .Q(out_r4));  // open: clr
  Register #(.width(32)) register_14 (.D(in_r12), .en(WE_12), .clk(in_6), .Q(out_r12));  // open: clr
  Register #(.width(32)) register_15 (.D(in_r20), .en(WE_20), .clk(in_6), .Q(out_r20));  // open: clr
  Register #(.width(32)) register_16 (.D(in_r28), .en(WE_28), .clk(in_6), .Q(out_r28));  // open: clr
  Demultiplexer #(.select(5), .width(32)) demultiplexer_1 (
    .out1(in_r1), .out2(in_r2), .out3(in_r3), .out4(in_r4), .out5(in_r5), .out6(in_r6), .out7(in_r7),
    .out8(in_r8), .out9(in_r9), .out10(in_r10), .out11(in_r11), .out12(in_r12), .out13(in_r13),
    .out14(in_r14), .out15(in_r15), .out16(in_r16), .out17(in_r17), .out18(in_r18), .out19(in_r19),
    .out20(in_r20), .out21(in_r21), .out22(in_r22), .out23(in_r23), .out24(in_r24), .out25(in_r25),
    .out26(in_r26), .out27(in_r27), .out28(in_r28), .out29(in_r29), .out30(in_r30), .out31(in_r31),
    .in(DataD), .sel(AddrD), .en(in_5));  // open: out0
  Register #(.width(32)) register_17 (.D(in_r5), .en(WE_5), .clk(in_6), .Q(out_r5));  // open: clr
  Register #(.width(32)) register_18 (.D(in_r13), .en(WE_13), .clk(in_6), .Q(out_r13));  // open: clr
  Register #(.width(32)) register_19 (.D(in_r21), .en(WE_21), .clk(in_6), .Q(out_r21));  // open: clr
  Register #(.width(32)) register_20 (.D(in_r29), .en(WE_29), .clk(in_6), .Q(out_r29));  // open: clr
  Register #(.width(32)) register_21 (.D(in_r6), .en(WE_6), .clk(in_6), .Q(out_r6));  // open: clr
  Register #(.width(32)) register_22 (.D(in_r14), .en(WE_14), .clk(in_6), .Q(out_r14));  // open: clr
  Register #(.width(32)) register_23 (.D(in_r22), .en(WE_22), .clk(in_6), .Q(out_r22));  // open: clr
  Register #(.width(32)) register_24 (.D(in_r30), .en(WE_30), .clk(in_6), .Q(out_r30));  // open: clr
  Decoder #(.select(5)) decoder_1 (
    .out1(WE_1), .out2(WE_2), .out3(WE_3), .out4(WE_4), .out5(WE_5), .out6(WE_6), .out7(WE_7), .out8(WE_8),
    .out9(WE_9), .out10(WE_10), .out11(WE_11), .out12(WE_12), .out13(WE_13), .out14(WE_14), .out15(WE_15),
    .out16(WE_16), .out17(WE_17), .out18(WE_18), .out19(WE_19), .out20(WE_20), .out21(WE_21), .out22(WE_22),
    .out23(WE_23), .out24(WE_24), .out25(WE_25), .out26(WE_26), .out27(WE_27), .out28(WE_28), .out29(WE_29),
    .out30(WE_30), .out31(WE_31), .sel(AddrD), .en(in_5));  // open: out0
  Register #(.width(32)) register_25 (.D(in_r7), .en(WE_7), .clk(in_6), .Q(out_r7));  // open: clr
  Register #(.width(32)) register_26 (.D(in_r15), .en(WE_15), .clk(in_6), .Q(out_r15));  // open: clr
  Register #(.width(32)) register_27 (.D(in_r23), .en(WE_23), .clk(in_6), .Q(out_r23));  // open: clr
  Register #(.width(32)) register_28 (.D(in_r31), .en(WE_31), .clk(in_6), .Q(out_r31));  // open: clr
  Register #(.width(32)) register_29 (.D(in_r8), .en(WE_8), .clk(in_6), .Q(out_r8));  // open: clr
  Register #(.width(32)) register_30 (.D(in_r16), .en(WE_16), .clk(in_6), .Q(out_r16));  // open: clr
  Register #(.width(32)) register_31 (.D(in_r24), .en(WE_24), .clk(in_6), .Q(out_r24));  // open: clr

  // Other names for the same wires on the sheet: busA[31:0] = DataA; busB[31:0] = DataB; busW[31:0] = DataD;
  //   CLK = in_6; RA[4:0] = AddrA; RB[4:0] = AddrB; RW[4:0] = AddrD; WRITE_ENABLE = in_5

  // Notes on the sheet:
  //   Outputs
  //   I/O
  //   Inputs
  //   Register Reading
  //   Register Writing
  //   X0 HARDWIRED
endmodule

module ALU (
  input  [31:0] rs1,
  input  [31:0] rs2,
  input  [3:0] OP,
  output [31:0] R
);

  wire comparator_1_lt, comparator_2_lt;
  wire [31:0] o_add, o_and, o_or, o_sll, o_slt, o_sltu, o_sra, o_srl, o_sub, o_xor;

  Multiplexer #(.select(4), .width(32), .enable("false")) multiplexer_1 (
    .in0(o_add), .in1(o_sub), .in2(o_sll), .in3(o_slt), .in4(o_sltu), .in5(o_xor), .in6(o_srl), .in7(o_sra),
    .in8(o_or), .in9(o_and), .out(R), .sel(OP));  // open: in10, in11, in12, in13, in14, in15
  Adder #(.width(32)) adder_1 (.a(rs1), .b(rs2), .out(o_add));  // open: cin, cout
  Subtractor #(.width(32)) subtractor_1 (.a(rs1), .b(rs2), .out(o_sub));  // open: bin, bout
  Shifter #(.width(32)) shifter_1 (.in(rs1), .\dist (rs2[4:0]), .out(o_sll));
  Bit_Extender #(.in_width(1), .out_width(32)) bit_extender_1 (.out(o_slt));  // open: in
  Comparator #(.width(32)) comparator_1 (.a(rs1), .b(rs2), .lt(comparator_1_lt));  // open: gt, eq
  Bit_Extender #(.in_width(1), .out_width(32), .\type ("zero")) bit_extender_2 (.out(o_sltu));  // open: in
  Comparator #(.width(32)) comparator_2 (.a(rs1), .b(rs2), .lt(comparator_2_lt));  // open: gt, eq
  assign o_xor = rs1 ^ rs2;  // XOR_Gate xor_1, 32 bits wide
  Shifter #(.width(32), .shift("lr")) shifter_2 (.in(rs1), .\dist (rs2[4:0]), .out(o_srl));
  Shifter #(.width(32), .shift("ar")) shifter_3 (.in(rs1), .\dist (rs2[4:0]), .out(o_sra));
  assign o_or = rs1 | rs2;  // OR_Gate or_1, 32 bits wide
  assign o_and = rs1 & rs2;  // AND_Gate and_1, 32 bits wide

  // Other names for the same wires on the sheet: result[31:0] = R; X[31:0] = rs1; Y[31:0] = rs2

  // Notes on the sheet:
  //   Outputs
  //   I/O
  //   Operation Selection
  //   Inputs
  //   Operations
endmodule

module DMEM (
  input  [31:0] ADDR,
  input  MemRW,
  input  CLK,
  input  [31:0] DataW,
  output [31:0] DataR
);

  RAM #(.addrWidth(24), .dataWidth(32), .trigger("falling"), .databus("bibus")) ram_1 (
    .addr(ADDR[25:2]), .we(MemRW), .oe(1'b1), .clk(CLK), .din(DataW), .dout(DataR));

  // Notes on the sheet:
  //   RAM
endmodule

module CONTROL_LOGIC (
  input  [31:0] Inst,
  output [6:0] out_2,
  output [4:0] out_3,
  output [2:0] out_4,
  output [4:0] out_5,
  output [4:0] out_6,
  output [6:0] out_7,
  output RegWEn,
  output [3:0] ALUSel
);

  wire comparator_2_eq, comparator_3_eq, comparator_4_eq, comparator_5_eq, comparator_6_eq, comparator_7_eq,
       comparator_8_eq, comparator_9_eq, comparator_10_eq, comparator_11_eq, comparator_12_eq,
       comparator_13_eq, comparator_14_eq, comparator_15_eq, comparator_16_eq, comparator_17_eq,
       comparator_18_eq, comparator_19_eq, comparator_20_eq, comparator_21_eq, R_add, R_and, R_or, R_sll,
       R_slt, R_sltu, R_sra, R_srl, R_sub, R_xor;

  Comparator #(.width(7)) comparator_1 (.a(Inst[6:0]), .b(7'b0110011), .eq(RegWEn));  // open: gt, lt
  Priority_Encoder #(.select(4)) priority_encoder_1 (
    .in0(R_add), .in1(R_sub), .in2(R_sll), .in3(R_slt), .in4(R_sltu), .in5(R_xor), .in6(R_srl), .in7(R_sra),
    .in8(R_or), .in9(R_and), .out(ALUSel));  // open: in10, in11, in12, in13, in14, in15, gs, en_out, en_in
  Comparator #(.width(3)) comparator_2 (.a(Inst[14:12]), .b(3'b000), .eq(comparator_2_eq));  // open: gt, lt
  Comparator #(.width(7)) comparator_3 (.a(Inst[31:25]), .b({7{1'b0}}), .eq(comparator_3_eq));  // open: gt, lt
  Comparator #(.width(3)) comparator_4 (.a(Inst[14:12]), .b(3'b000), .eq(comparator_4_eq));  // open: gt, lt
  Comparator #(.width(7)) comparator_5 (.a(Inst[31:25]), .b(7'b0100000), .eq(comparator_5_eq));  // open: gt, lt
  Comparator #(.width(3)) comparator_6 (.a(Inst[14:12]), .b(3'b001), .eq(comparator_6_eq));  // open: gt, lt
  Comparator #(.width(7)) comparator_7 (.a(Inst[31:25]), .b({7{1'b0}}), .eq(comparator_7_eq));  // open: gt, lt
  Comparator #(.width(3)) comparator_8 (.a(Inst[14:12]), .b(3'b010), .eq(comparator_8_eq));  // open: gt, lt
  Comparator #(.width(7)) comparator_9 (.a(Inst[31:25]), .b({7{1'b0}}), .eq(comparator_9_eq));  // open: gt, lt
  Comparator #(.width(3)) comparator_10 (.a(Inst[14:12]), .b(3'b011), .eq(comparator_10_eq));  // open: gt, lt
  Comparator #(.width(7)) comparator_11 (.a(Inst[31:25]), .b({7{1'b0}}), .eq(comparator_11_eq));  // open: gt, lt
  and and_1 (R_add, RegWEn, comparator_2_eq, comparator_3_eq);
  and and_2 (R_sub, RegWEn, comparator_4_eq, comparator_5_eq);
  and and_3 (R_sll, RegWEn, comparator_6_eq, comparator_7_eq);
  and and_4 (R_slt, RegWEn, comparator_8_eq, comparator_9_eq);
  and and_5 (R_sltu, RegWEn, comparator_10_eq, comparator_11_eq);
  Comparator #(.width(3)) comparator_12 (.a(Inst[14:12]), .b(3'b100), .eq(comparator_12_eq));  // open: gt, lt
  Comparator #(.width(7)) comparator_13 (.a(Inst[31:25]), .b({7{1'b0}}), .eq(comparator_13_eq));  // open: gt, lt
  Comparator #(.width(3)) comparator_14 (.a(Inst[14:12]), .b(3'b101), .eq(comparator_14_eq));  // open: gt, lt
  Comparator #(.width(7)) comparator_15 (.a(Inst[31:25]), .b({7{1'b0}}), .eq(comparator_15_eq));  // open: gt, lt
  Comparator #(.width(3)) comparator_16 (.a(Inst[14:12]), .b(3'b101), .eq(comparator_16_eq));  // open: gt, lt
  Comparator #(.width(7)) comparator_17 (.a(Inst[31:25]), .b(7'b0100000), .eq(comparator_17_eq));  // open: gt, lt
  Comparator #(.width(3)) comparator_18 (.a(Inst[14:12]), .b(3'b110), .eq(comparator_18_eq));  // open: gt, lt
  Comparator #(.width(7)) comparator_19 (.a(Inst[31:25]), .b({7{1'b0}}), .eq(comparator_19_eq));  // open: gt, lt
  Comparator #(.width(3)) comparator_20 (.a(Inst[14:12]), .b(3'b111), .eq(comparator_20_eq));  // open: gt, lt
  Comparator #(.width(7)) comparator_21 (.a(Inst[31:25]), .b({7{1'b0}}), .eq(comparator_21_eq));  // open: gt, lt
  and and_6 (R_xor, RegWEn, comparator_12_eq, comparator_13_eq);
  and and_7 (R_srl, RegWEn, comparator_14_eq, comparator_15_eq);
  and and_8 (R_sra, RegWEn, comparator_16_eq, comparator_17_eq);
  and and_9 (R_or, RegWEn, comparator_18_eq, comparator_19_eq);
  and and_10 (R_and, RegWEn, comparator_20_eq, comparator_21_eq);

  assign out_2 = Inst[6:0];
  assign out_3 = Inst[11:7];
  assign out_4 = Inst[14:12];
  assign out_5 = Inst[19:15];
  assign out_6 = Inst[24:20];
  assign out_7 = Inst[31:25];

  // Other names for the same wires on the sheet: ALU_OP[3:0] = ALUSel; OPCODE[6:0] = Inst[6:0]; RD[4:0] = Inst[11:7];
  //   FUNCT3[2:0] = Inst[14:12]; RS1[4:0] = Inst[19:15]; RS2[4:0] = Inst[24:20]; FUNCT7[6:0] = Inst[31:25];
  //   R_TYPE = RegWEn

  // Notes on the sheet:
  //   EXECUTE
  //   ALU Operation Encoding
  //   INSTRUCTION DECODING
  //   R-TYPE
  //   WRITE BACK
  //   Register Write Enable
endmodule

module ID_EX (
  input  RegWEn,
  input  [3:0] ALUSel,
  input  CLK,
  output RegWEnOut,
  output [3:0] ALUSelOut
);

  Register #(.width(1)) register_1 (.D(RegWEn), .en(CLK), .Q(RegWEnOut));  // open: clk, clr
  Register #(.width(4)) register_2 (.D(ALUSel), .en(CLK), .Q(ALUSelOut));  // open: clk, clr

  // Notes on the sheet:
  //   WB
  //   MEM
  //   EX
endmodule
