// Logisim project RV32I_pipelined_attempt1.circ as structural Verilog: 12 circuits, main circuit main
module main (
  input  in_1,
  output [6:0] out_2,
  output [4:0] out_3,
  output [2:0] out_4,
  output [4:0] out_5,
  output [6:0] out_6,
  output [31:0] out_7,
  output [4:0] out_8,
  output [31:0] out_9
);

  wire Asel, BrTaken, BSel, CLK, ex_mem_1_memrwout, ex_mem_1_pcselout, ex_mem_1_regwenout, id_ex_1_aselout,
       id_ex_1_bselout, id_ex_1_memrwout, id_ex_1_pcselout, id_ex_1_regwenout, mem_wb_1_regwenout, MemRW,
       PCSel, RegWEn;
  wire [1:0] ex_mem_1_wbselout, id_ex_1_wbselout, mem_wb_1_wbselout, WBSel;
  wire [2:0] id_ex_1_funct3out, id_ex_1_immselout, ImmSel;
  wire [3:0] ALUSel, id_ex_1_aluselout;
  wire [31:0] adder_1_out, adder_2_out, alu_1_r, ALUmem_q, dmem_1_datar, imem_1_inst, imm_gen_1_imm, IMMex_q,
       INSTRUCTION, multiplexer_1_out, multiplexer_2_out, multiplexer_3_out, multiplexer_4_out, PC_plus4wb_q,
       PCex_q, PCid_q, PCmem_q, regfile_1_dataa, regfile_1_datab, register_1_q, RS1ex_q, RS2ex_q, RS2mem_q;

  Register #(.width(32)) register_1 (.D(multiplexer_1_out), .clk(CLK), .Q(register_1_q), .clr(in_1));  // open: en
  Multiplexer #(.width(32), .enable("false")) multiplexer_1 (
    .in0(adder_1_out), .in1(ALUmem_q), .out(multiplexer_1_out), .sel(ex_mem_1_pcselout));
  Adder #(.width(32)) adder_1 (.a(32'h4), .b(register_1_q), .out(adder_1_out));  // open: cin, cout
  CONTROL_LOGIC control_logic_1 (
    .Inst(INSTRUCTION), .BrTaken(BrTaken), .out_3(out_2), .out_4(out_3), .out_5(out_4), .out_6(out_5),
    .out_7(out_8), .out_8(out_6), .RegWEn(RegWEn), .ASel(Asel), .BSel(BSel), .ImmSel(ImmSel),
    .ALUSel(ALUSel), .WBSel(WBSel), .MemRW(MemRW), .PCSel(PCSel));
  Register #(.width(32)) PCid (.D(register_1_q), .Q(PCid_q));  // open: en, clk, clr
  Register #(.width(32)) INSTid (.D(imem_1_inst), .Q(INSTRUCTION));  // open: en, clk, clr
  IMEM imem_1 (.ADDR(register_1_q), .INST(imem_1_inst));
  ID_EX id_ex_1 (
    .RegWEn(RegWEn), .WBSel(WBSel), .MemRW(MemRW), .PCSel(PCSel), .ASel(Asel), .BSel(BSel), .ALUSel(ALUSel),
    .ImmSel(ImmSel), .Funct3(out_4), .CLK(CLK), .RegWEnout(id_ex_1_regwenout), .WBSelout(id_ex_1_wbselout),
    .MemRWout(id_ex_1_memrwout), .PCSelout(id_ex_1_pcselout), .ASelout(id_ex_1_aselout),
    .BSelout(id_ex_1_bselout), .ALUSelout(id_ex_1_aluselout), .ImmSelout(id_ex_1_immselout),
    .Funct3out(id_ex_1_funct3out));
  Register #(.width(32)) PCex (.D(PCid_q), .clk(CLK), .Q(PCex_q));  // open: en, clr
  Register #(.width(32)) RS1ex (.D(regfile_1_dataa), .clk(CLK), .Q(RS1ex_q));  // open: en, clr
  RegFile regfile_1 (
    .DataD(multiplexer_4_out), .AddrD(INSTRUCTION[11:7]), .AddrA(INSTRUCTION[19:15]),
    .AddrB(INSTRUCTION[24:20]), .in_5(mem_wb_1_regwenout), .in_6(CLK), .DataA(regfile_1_dataa),
    .DataB(regfile_1_datab));
  Register #(.width(32)) RS2ex (.D(regfile_1_datab), .clk(CLK), .Q(RS2ex_q));  // open: en, clr
  Register #(.width(32)) IMMex (.D(imm_gen_1_imm), .clk(CLK), .Q(IMMex_q));  // open: en, clr
  Imm_Gen imm_gen_1 (.Inst(INSTRUCTION), .ImmSel(id_ex_1_immselout), .Imm(imm_gen_1_imm));
  Clock clock_1 (.out(CLK));
  Branch_Comp branch_comp_1 (.A(RS1ex_q), .B(RS2ex_q), .FUNCT3(id_ex_1_funct3out), .out_4(BrTaken));
  Multiplexer #(.select(2), .width(32), .enable("false")) multiplexer_2 (
    .in0(RS1ex_q), .in1(PCex_q), .in2(multiplexer_4_out), .in3(ALUmem_q), .out(multiplexer_2_out));  // open: sel
  Multiplexer #(.select(2), .width(32), .enable("false")) multiplexer_3 (
    .in0(RS2ex_q), .in1(IMMex_q), .in2(multiplexer_4_out), .in3(ALUmem_q), .out(multiplexer_3_out));  // open: sel
  ALU alu_1 (.rs1(multiplexer_2_out), .rs2(multiplexer_3_out), .OP(id_ex_1_aluselout), .R(alu_1_r));
  Register #(.width(32)) PCmem (.D(PCex_q), .clk(CLK), .Q(PCmem_q));  // open: en, clr
  Register #(.width(32)) ALUmem (.D(alu_1_r), .clk(CLK), .Q(ALUmem_q));  // open: en, clr
  Register #(.width(32)) RS2mem (.D(RS2ex_q), .clk(CLK), .Q(RS2mem_q));  // open: en, clr
  EX_MEM ex_mem_1 (
    .RegWEn(id_ex_1_regwenout), .WBSel(id_ex_1_wbselout), .MemRW(id_ex_1_memrwout), .PCSel(id_ex_1_pcselout),
    .CLK(CLK), .RegWEnout(ex_mem_1_regwenout), .WBSelout(ex_mem_1_wbselout), .MemRWout(ex_mem_1_memrwout),
    .PCSelout(ex_mem_1_pcselout));
  Adder #(.width(32)) adder_2 (.a(32'h4), .b(PCmem_q), .out(adder_2_out));  // open: cin, cout
  DMEM dmem_1 (.ADDR(ALUmem_q), .MemRW(ex_mem_1_memrwout), .CLK(CLK), .DataW(RS2mem_q), .DataR(dmem_1_datar));
  Register #(.width(32)) PC_plus4wb (.D(adder_2_out), .clk(CLK), .Q(PC_plus4wb_q));  // open: en, clr
  Register #(.width(32)) ALUwb (.D(ALUmem_q), .clk(CLK), .Q(out_7));  // open: en, clr
  Register #(.width(32)) MEMwb (.D(dmem_1_datar), .clk(CLK), .Q(out_9));  // open: en, clr
  MEM_WB mem_wb_1 (
    .RegWEn(ex_mem_1_regwenout), .WBSel(ex_mem_1_wbselout), .CLK(CLK), .RegWEnout(mem_wb_1_regwenout),
    .WBSELout(mem_wb_1_wbselout));
  Multiplexer #(.select(2), .width(32), .enable("false")) multiplexer_4 (
    .in0(out_9), .in1(out_7), .in2(PC_plus4wb_q), .out(multiplexer_4_out), .sel(mem_wb_1_wbselout));  // open: in3

  // Other names for the same wires on the sheet: ALU_Out[31:0] = out_7; FUNCT3[2:0] = out_4; FUNCT7[6:0] = out_6;
  //   Memory_Out[31:0] = out_9; OPCODE[6:0] = out_2; RD[4:0] = out_3; RS1[4:0] = out_5; RS2[4:0] = out_8

  // Notes on the sheet:
  //   CONTROL LOGIC
  //   USER INTERFACE
endmodule

module IMEM (
  input  [31:0] ADDR,
  output [31:0] INST
);

  ROM #(.addrWidth(24), .dataWidth(32)) rom_1 (.addr(ADDR[25:2]), .data(INST));

  // Notes on the sheet:
  //   ROM
  //   contents of rom_1 (hex, n*v repeats v):
  //   2b3 100313 10000e17 ff8e0e13 e2e03 e0c63 5303b3 30293 38313 fffe0e13 fedff06f 100513 28593 73 a00513
  //   73 10000e17 fc0e0e13 5e2223
endmodule

module RegFile (
  input  [31:0] DataD,
  input  [4:0] AddrD,
  input  [4:0] AddrA,
  input  [4:0] AddrB,
  input  in_5,
  input  in_6,
  output [31:0] DataA,
  output [31:0] DataB
);

  wire WE_1, WE_2, WE_3, WE_4, WE_5, WE_6, WE_7, WE_8, WE_9, WE_10, WE_11, WE_12, WE_13, WE_14, WE_15, WE_16,
       WE_17, WE_18, WE_19, WE_20, WE_21, WE_22, WE_23, WE_24, WE_25, WE_26, WE_27, WE_28, WE_29, WE_30,
       WE_31;
  wire [31:0] in_r1, in_r2, in_r3, in_r4, in_r5, in_r6, in_r7, in_r8, in_r9, in_r10, in_r11, in_r12, in_r13,
       in_r14, in_r15, in_r16, in_r17, in_r18, in_r19, in_r20, in_r21, in_r22, in_r23, in_r24, in_r25,
       in_r26, in_r27, in_r28, in_r29, in_r30, in_r31, out_r1, out_r2, out_r3, out_r4, out_r5, out_r6,
       out_r7, out_r8, out_r9, out_r10, out_r11, out_r12, out_r13, out_r14, out_r15, out_r16, out_r17,
       out_r18, out_r19, out_r20, out_r21, out_r22, out_r23, out_r24, out_r25, out_r26, out_r27, out_r28,
       out_r29, out_r30, out_r31;

  Register #(.width(32)) register_1 (.D(in_r1), .en(WE_1), .clk(in_6), .Q(out_r1));  // open: clr
  Register #(.width(32)) register_2 (.D(in_r9), .en(WE_9), .clk(in_6), .Q(out_r9));  // open: clr
  Register #(.width(32)) register_3 (.D(in_r17), .en(WE_17), .clk(in_6), .Q(out_r17));  // open: clr
  Register #(.width(32)) register_4 (.D(in_r25), .en(WE_25), .clk(in_6), .Q(out_r25));  // open: clr
  Multiplexer #(.select(5), .width(32), .enable("false")) multiplexer_1 (
    .in0({32{1'b0}}), .in1(out_r1), .in2(out_r2), .in3(out_r3), .in4(out_r4), .in5(out_r5), .in6(out_r6),
    .in7(out_r7), .in8(out_r8), .in9(out_r9), .in10(out_r10), .in11(out_r11), .in12(out_r12), .in13(out_r13),
    .in14(out_r14), .in15(out_r15), .in16(out_r16), .in17(out_r17), .in18(out_r18), .in19(out_r19),
    .in20(out_r20), .in21(out_r21), .in22(out_r22), .in23(out_r23), .in24(out_r24), .in25(out_r25),
    .in26(out_r26), .in27(out_r27), .in28(out_r28), .in29(out_r29), .in30(out_r30), .in31(out_r31),
    .out(DataA), .sel(AddrA));
  Register #(.width(32)) register_5 (.D(in_r2), .en(WE_2), .clk(in_6), .Q(out_r2));  // open: clr
  Register #(.width(32)) register_6 (.D(in_r10), .en(WE_10), .clk(in_6), .Q(out_r10));  // open: clr
  Register #(.width(32)) register_7 (.D(in_r18), .en(WE_18), .clk(in_6), .Q(out_r18));  // open: clr
  Register #(.width(32)) register_8 (.D(in_r26), .en(WE_26), .clk(in_6), .Q(out_r26));  // open: clr
  Register #(.width(32)) register_9 (.D(in_r3), .en(WE_3), .clk(in_6), .Q(out_r3));  // open: clr
  Register #(.width(32)) register_10 (.D(in_r11), .en(WE_11), .clk(in_6), .Q(out_r11));  // open: clr
  Register #(.width(32)) register_11 (.D(in_r19), .en(WE_19), .clk(in_6), .Q(out_r19));  // open: clr
  Register #(.width(32)) register_12 (.D(in_r27), .en(WE_27), .clk(in_6), .Q(out_r27));  // open: clr
  Multiplexer #(.select(5), .width(32), .enable("false")) multiplexer_2 (
    .in0({32{1'b0}}), .in1(out_r1), .in2(out_r2), .in3(out_r3), .in4(out_r4), .in5(out_r5), .in6(out_r6),
    .in7(out_r7), .in8(out_r8), .in9(out_r9), .in10(out_r10), .in11(out_r11), .in12(out_r12), .in13(out_r13),
    .in14(out_r14), .in15(out_r15), .in16(out_r16), .in17(out_r17), .in18(out_r18), .in19(out_r19),
    .in20(out_r20), .in21(out_r21), .in22(out_r22), .in23(out_r23), .in24(out_r24), .in25(out_r25),
    .in26(out_r26), .in27(out_r27), .in28(out_r28), .in29(out_r29), .in30(out_r30), .in31(out_r31),
    .out(DataB), .sel(AddrB));
  Register #(.width(32)) register_13 (.D(in_r4), .en(WE_4), .clk(in_6), .Q(out_r4));  // open: clr
  Register #(.width(32)) register_14 (.D(in_r12), .en(WE_12), .clk(in_6), .Q(out_r12));  // open: clr
  Register #(.width(32)) register_15 (.D(in_r20), .en(WE_20), .clk(in_6), .Q(out_r20));  // open: clr
  Register #(.width(32)) register_16 (.D(in_r28), .en(WE_28), .clk(in_6), .Q(out_r28));  // open: clr
  Demultiplexer #(.select(5), .width(32)) demultiplexer_1 (
    .out1(in_r1), .out2(in_r2), .out3(in_r3), .out4(in_r4), .out5(in_r5), .out6(in_r6), .out7(in_r7),
    .out8(in_r8), .out9(in_r9), .out10(in_r10), .out11(in_r11), .out12(in_r12), .out13(in_r13),
    .out14(in_r14), .out15(in_r15), .out16(in_r16), .out17(in_r17), .out18(in_r18), .out19(in_r19),
    .out20(in_r20), .out21(in_r21), .out22(in_r22), .out23(in_r23), .out24(in_r24), .out25(in_r25),
    .out26(in_r26), .out27(in_r27), .out28(in_r28), .out29(in_r29), .out30(in_r30), .out31(in_r31),
    .in(DataD), .sel(AddrD), .en(in_5));  // open: out0
  Register #(.width(32)) register_17 (.D(in_r5), .en(WE_5), .clk(in_6), .Q(out_r5));  // open: clr
  Register #(.width(32)) register_18 (.D(in_r13), .en(WE_13), .clk(in_6), .Q(out_r13));  // open: clr
  Register #(.width(32)) register_19 (.D(in_r21), .en(WE_21), .clk(in_6), .Q(out_r21));  // open: clr
  Register #(.width(32)) register_20 (.D(in_r29), .en(WE_29), .clk(in_6), .Q(out_r29));  // open: clr
  Register #(.width(32)) register_21 (.D(in_r6), .en(WE_6), .clk(in_6), .Q(out_r6));  // open: clr
  Register #(.width(32)) register_22 (.D(in_r14), .en(WE_14), .clk(in_6), .Q(out_r14));  // open: clr
  Register #(.width(32)) register_23 (.D(in_r22), .en(WE_22), .clk(in_6), .Q(out_r22));  // open: clr
  Register #(.width(32)) register_24 (.D(in_r30), .en(WE_30), .clk(in_6), .Q(out_r30));  // open: clr
  Decoder #(.select(5)) decoder_1 (
    .out1(WE_1), .out2(WE_2), .out3(WE_3), .out4(WE_4), .out5(WE_5), .out6(WE_6), .out7(WE_7), .out8(WE_8),
    .out9(WE_9), .out10(WE_10), .out11(WE_11), .out12(WE_12), .out13(WE_13), .out14(WE_14), .out15(WE_15),
    .out16(WE_16), .out17(WE_17), .out18(WE_18), .out19(WE_19), .out20(WE_20), .out21(WE_21), .out22(WE_22),
    .out23(WE_23), .out24(WE_24), .out25(WE_25), .out26(WE_26), .out27(WE_27), .out28(WE_28), .out29(WE_29),
    .out30(WE_30), .out31(WE_31), .sel(AddrD), .en(in_5));  // open: out0
  Register #(.width(32)) register_25 (.D(in_r7), .en(WE_7), .clk(in_6), .Q(out_r7));  // open: clr
  Register #(.width(32)) register_26 (.D(in_r15), .en(WE_15), .clk(in_6), .Q(out_r15));  // open: clr
  Register #(.width(32)) register_27 (.D(in_r23), .en(WE_23), .clk(in_6), .Q(out_r23));  // open: clr
  Register #(.width(32)) register_28 (.D(in_r31), .en(WE_31), .clk(in_6), .Q(out_r31));  // open: clr
  Register #(.width(32)) register_29 (.D(in_r8), .en(WE_8), .clk(in_6), .Q(out_r8));  // open: clr
  Register #(.width(32)) register_30 (.D(in_r16), .en(WE_16), .clk(in_6), .Q(out_r16));  // open: clr
  Register #(.width(32)) register_31 (.D(in_r24), .en(WE_24), .clk(in_6), .Q(out_r24));  // open: clr

  // Other names for the same wires on the sheet: busA[31:0] = DataA; busB[31:0] = DataB; busW[31:0] = DataD;
  //   CLK = in_6; RA[4:0] = AddrA; RB[4:0] = AddrB; RW[4:0] = AddrD; WRITE_ENABLE = in_5

  // Notes on the sheet:
  //   Outputs
  //   I/O
  //   Inputs
  //   Register Reading
  //   Register Writing
  //   X0 HARDWIRED
endmodule

module ALU (
  input  [31:0] rs1,
  input  [31:0] rs2,
  input  [3:0] OP,
  output [31:0] R
);

  wire comparator_1_lt, comparator_2_lt;
  wire [31:0] o_add, o_and, o_copyrs2, o_or, o_sll, o_slt, o_sltu, o_sra, o_srl, o_sub, o_xor;

  Multiplexer #(.select(4), .width(32), .enable("false")) multiplexer_1 (
    .in0(o_add), .in1(o_sub), .in2(o_sll), .in3(o_slt), .in4(o_sltu), .in5(o_xor), .in6(o_srl), .in7(o_sra),
    .in8(o_or), .in9(o_and), .in10(o_copyrs2), .out(R), .sel(OP));  // open: in11, in12, in13, in14, in15
  Adder #(.width(32)) adder_1 (.a(rs1), .b(rs2), .out(o_add));  // open: cin, cout
  Subtractor #(.width(32)) subtractor_1 (.a(rs1), .b(rs2), .out(o_sub));  // open: bin, bout
  Shifter #(.width(32)) shifter_1 (.in(rs1), .\dist (rs2[4:0]), .out(o_sll));
  Bit_Extender #(.in_width(1), .out_width(32)) bit_extender_1 (.out(o_slt));  // open: in
  Comparator #(.width(32)) comparator_1 (.a(rs1), .b(rs2), .lt(comparator_1_lt));  // open: gt, eq
  Bit_Extender #(.in_width(1), .out_width(32), .\type ("zero")) bit_extender_2 (.out(o_sltu));  // open: in
  Comparator #(.width(32)) comparator_2 (.a(rs1), .b(rs2), .lt(comparator_2_lt));  // open: gt, eq
  assign o_xor = rs1 ^ rs2;  // XOR_Gate xor_1, 32 bits wide
  Shifter #(.width(32), .shift("lr")) shifter_2 (.in(rs1), .\dist (rs2[4:0]), .out(o_srl));
  Shifter #(.width(32), .shift("ar")) shifter_3 (.in(rs1), .\dist (rs2[4:0]), .out(o_sra));
  assign o_or = rs1 | rs2;  // OR_Gate or_1, 32 bits wide
  assign o_and = rs1 & rs2;  // AND_Gate and_1, 32 bits wide
  Adder #(.width(32)) adder_2 (.a({32{1'b0}}), .b(rs2), .out(o_copyrs2));  // open: cin, cout

  // Other names for the same wires on the sheet: result[31:0] = R; X[31:0] = rs1; Y[31:0] = rs2

  // Notes on the sheet:
  //   Outputs
  //   I/O
  //   Operation Selection
  //   Inputs
  //   Operations
endmodule

module DMEM (
  input  [31:0] ADDR,
  input  MemRW,
  input  CLK,
  input  [31:0] DataW,
  output [31:0] DataR
);

  RAM #(.addrWidth(24), .dataWidth(32), .trigger("falling"), .databus("bibus")) ram_1 (
    .addr(ADDR[25:2]), .we(MemRW), .oe(1'b1), .clk(CLK), .din(DataW), .dout(DataR));

  // Notes on the sheet:
  //   RAM
endmodule

module CONTROL_LOGIC (
  input  [31:0] Inst,
  input  BrTaken,
  output [6:0] out_3,
  output [4:0] out_4,
  output [2:0] out_5,
  output [4:0] out_6,
  output [4:0] out_7,
  output [6:0] out_8,
  output RegWEn,
  output ASel,
  output BSel,
  output [2:0] ImmSel,
  output [3:0] ALUSel,
  output [1:0] WBSel,
  output MemRW,
  output PCSel
);

  wire and_1_out, and_2_out, and_3_out, and_4_out, and_5_out, and_6_out, B_beq, B_bge, B_bgeu, B_blt, B_bltu,
       B_bne, B_TYPE, comparator_10_eq, comparator_11_eq, comparator_12_eq, comparator_13_eq,
       comparator_14_eq, comparator_15_eq, comparator_16_eq, comparator_17_eq, comparator_18_eq,
       comparator_19_eq, comparator_20_eq, comparator_21_eq, comparator_22_eq, comparator_23_eq,
       comparator_24_eq, comparator_25_eq, comparator_26_eq, comparator_27_eq, comparator_28_eq,
       comparator_29_eq, comparator_30_eq, comparator_31_eq, comparator_32_eq, comparator_33_eq,
       comparator_34_eq, comparator_35_eq, comparator_36_eq, comparator_37_eq, comparator_38_eq,
       comparator_39_eq, comparator_40_eq, comparator_41_eq, comparator_42_eq, comparator_43_eq,
       comparator_44_eq, comparator_45_eq, comparator_46_eq, comparator_47_eq, comparator_48_eq,
       comparator_49_eq, comparator_50_eq, comparator_51_eq, comparator_52_eq, comparator_53_eq,
       comparator_54_eq, comparator_55_eq, comparator_56_eq, comparator_57_eq, comparator_58_eq,
       comparator_59_eq, comparator_60_eq, comparator_61_eq, I_add, I_and, I_jalr, I_lb, I_lbu, I_lh, I_lhu,
       I_lw, I_or, I_sll, I_slt, I_sltu, I_sra, I_srl, I_TYPE, I_TYPE_LOAD, I_xor, J_TYPE, or_1_out,
       or_2_out, or_3_out, or_4_out, or_5_out, or_6_out, or_7_out, or_8_out, or_9_out, or_10_out, or_11_out,
       or_12_out, or_14_out, or_15_out, or_17_out, or_18_out, or_19_out, or_20_out, or_21_out, or_22_out,
       or_23_out, or_24_out, or_26_out, R_add, R_and, R_or, R_sll, R_slt, R_sltu, R_sra, R_srl, R_sub,
       R_TYPE, R_xor, S_sb, S_sh, S_sw, S_TYPE, U_TYPE, U_TYPE_AUIPC, U_TYPE_LUI;

  or or_1 (or_1_out, I_jalr, J_TYPE);
  or or_2 (or_2_out, R_sll, I_sll);
  or or_3 (or_3_out, R_slt, I_slt);
  or or_4 (or_4_out, R_sltu, I_sltu);
  or or_5 (or_5_out, R_xor, I_xor);
  or or_6 (or_6_out, R_srl, I_srl);
  or or_7 (or_7_out, R_sra, I_sra);
  or or_8 (or_8_out, R_or, I_or);
  or or_9 (or_9_out, R_and, I_and);
  or or_10 (or_10_out, R_add, I_add, S_TYPE, B_TYPE, or_1_out);
  or or_11 (or_11_out, or_10_out, or_12_out);
  Comparator #(.width(7)) comparator_1 (.a(Inst[6:0]), .b(7'b0110011), .eq(R_TYPE));  // open: gt, lt
  Comparator #(.width(7)) comparator_2 (.a(Inst[6:0]), .b(7'b0010011), .eq(I_TYPE));  // open: gt, lt
  Comparator #(.width(7)) comparator_3 (.a(Inst[6:0]), .b(7'b0000011), .eq(I_TYPE_LOAD));  // open: gt, lt
  Comparator #(.width(7)) comparator_4 (.a(Inst[6:0]), .b(7'b0100011), .eq(S_TYPE));  // open: gt, lt
  Comparator #(.width(7)) comparator_5 (.a(Inst[6:0]), .b(7'b1100011), .eq(B_TYPE));  // open: gt, lt
  Comparator #(.width(7)) comparator_6 (.a(Inst[6:0]), .b(7'b1100111), .eq(I_jalr));  // open: gt, lt
  Comparator #(.width(7)) comparator_7 (.a(Inst[6:0]), .b(7'b1101111), .eq(J_TYPE));  // open: gt, lt
  Comparator #(.width(7)) comparator_8 (.a(Inst[6:0]), .b(7'b0010111), .eq(U_TYPE_AUIPC));  // open: gt, lt
  Comparator #(.width(7)) comparator_9 (.a(Inst[6:0]), .b(7'b0110111), .eq(U_TYPE_LUI));  // open: gt, lt
  or or_12 (or_12_out, U_TYPE_AUIPC, I_TYPE_LOAD);
  Priority_Encoder #(.select(4)) priority_encoder_1 (
    .in0(or_11_out), .in1(R_sub), .in2(or_2_out), .in3(or_3_out), .in4(or_4_out), .in5(or_5_out),
    .in6(or_6_out), .in7(or_7_out), .in8(or_8_out), .in9(or_9_out), .in10(U_TYPE_LUI), .out(ALUSel));  // open: in11, in12, in13, in14, in15, gs, en_out, en_in
  or or_13 (U_TYPE, U_TYPE_AUIPC, U_TYPE_LUI);
  and and_1 (and_1_out, B_beq, BrTaken);
  and and_2 (and_2_out, B_bne, BrTaken);
  and and_3 (and_3_out, B_blt, BrTaken);
  and and_4 (and_4_out, B_bge, BrTaken);
  and and_5 (and_5_out, B_bltu, BrTaken);
  and and_6 (and_6_out, B_bgeu, BrTaken);
  or or_14 (or_14_out, and_1_out, and_2_out, and_3_out, and_4_out, and_5_out, and_6_out);
  or or_15 (or_15_out, I_jalr, J_TYPE);
  Comparator #(.width(3)) comparator_10 (.a(Inst[14:12]), .b(3'b000), .eq(comparator_10_eq));  // open: gt, lt
  Comparator #(.width(7)) comparator_11 (.a(Inst[31:25]), .b({7{1'b0}}), .eq(comparator_11_eq));  // open: gt, lt
  Comparator #(.width(3)) comparator_12 (.a(Inst[14:12]), .b(3'b000), .eq(comparator_12_eq));  // open: gt, lt
  Comparator #(.width(7)) comparator_13 (.a(Inst[31:25]), .b(7'b0100000), .eq(comparator_13_eq));  // open: gt, lt
  Comparator #(.width(3)) comparator_14 (.a(Inst[14:12]), .b(3'b001), .eq(comparator_14_eq));  // open: gt, lt
  Comparator #(.width(7)) comparator_15 (.a(Inst[31:25]), .b({7{1'b0}}), .eq(comparator_15_eq));  // open: gt, lt
  Comparator #(.width(3)) comparator_16 (.a(Inst[14:12]), .b(3'b010), .eq(comparator_16_eq));  // open: gt, lt
  Comparator #(.width(7)) comparator_17 (.a(Inst[31:25]), .b({7{1'b0}}), .eq(comparator_17_eq));  // open: gt, lt
  Comparator #(.width(3)) comparator_18 (.a(Inst[14:12]), .b(3'b011), .eq(comparator_18_eq));  // open: gt, lt
  Comparator #(.width(7)) comparator_19 (.a(Inst[31:25]), .b({7{1'b0}}), .eq(comparator_19_eq));  // open: gt, lt
  or or_16 (PCSel, or_14_out, or_15_out);
  and and_7 (R_add, R_TYPE, comparator_10_eq, comparator_11_eq);
  and and_8 (R_sub, R_TYPE, comparator_12_eq, comparator_13_eq);
  and and_9 (R_sll, R_TYPE, comparator_14_eq, comparator_15_eq);
  and and_10 (R_slt, R_TYPE, comparator_16_eq, comparator_17_eq);
  and and_11 (R_sltu, R_TYPE, comparator_18_eq, comparator_19_eq);
  or or_17 (or_17_out, R_TYPE, I_TYPE_LOAD);
  or or_18 (or_18_out, I_TYPE, I_jalr);
  or or_19 (or_19_out, J_TYPE, U_TYPE);
  or or_20 (or_20_out, I_jalr, or_21_out);
  or or_21 (or_21_out, J_TYPE, I_TYPE_LOAD, U_TYPE);
  or or_22 (or_22_out, I_TYPE, I_TYPE_LOAD, I_jalr);
  or or_23 (or_23_out, R_TYPE, U_TYPE, I_TYPE);
  or or_24 (or_24_out, I_jalr, J_TYPE);
  or or_25 (RegWEn, or_17_out, or_18_out, or_19_out);
  or or_26 (or_26_out, I_TYPE, S_TYPE, B_TYPE, or_20_out);
  Priority_Encoder priority_encoder_2 (
    .in0(or_22_out), .in1(S_TYPE), .in2(B_TYPE), .in3(J_TYPE), .in4(U_TYPE), .out(ImmSel));  // open: in5, in6, in7, en_in, gs, en_out
  Priority_Encoder #(.select(2)) priority_encoder_3 (
    .in0(I_TYPE_LOAD), .in1(or_23_out), .in2(or_24_out), .out(WBSel));  // open: in3, gs, en_out, en_in
  or or_27 (MemRW, S_sw, S_sh, S_sb);
  Comparator #(.width(3)) comparator_20 (.a(Inst[14:12]), .b(3'b100), .eq(comparator_20_eq));  // open: gt, lt
  Comparator #(.width(7)) comparator_21 (.a(Inst[31:25]), .b({7{1'b0}}), .eq(comparator_21_eq));  // open: gt, lt
  Comparator #(.width(3)) comparator_22 (.a(Inst[14:12]), .b(3'b101), .eq(comparator_22_eq));  // open: gt, lt
  Comparator #(.width(7)) comparator_23 (.a(Inst[31:25]), .b({7{1'b0}}), .eq(comparator_23_eq));  // open: gt, lt
  Comparator #(.width(3)) comparator_24 (.a(Inst[14:12]), .b(3'b101), .eq(comparator_24_eq));  // open: gt, lt
  Comparator #(.width(7)) comparator_25 (.a(Inst[31:25]), .b(7'b0100000), .eq(comparator_25_eq));  // open: gt, lt
  Comparator #(.width(3)) comparator_26 (.a(Inst[14:12]), .b(3'b110), .eq(comparator_26_eq));  // open: gt, lt
  Comparator #(.width(7)) comparator_27 (.a(Inst[31:25]), .b({7{1'b0}}), .eq(comparator_27_eq));  // open: gt, lt
  Comparator #(.width(3)) comparator_28 (.a(Inst[14:12]), .b(3'b111), .eq(comparator_28_eq));  // open: gt, lt
  Comparator #(.width(7)) comparator_29 (.a(Inst[31:25]), .b({7{1'b0}}), .eq(comparator_29_eq));  // open: gt, lt
  or or_28 (ASel, U_TYPE_AUIPC, J_TYPE, B_TYPE);
  Priority_Encoder #(.select(1)) priority_encoder_4 (
    .in0(R_TYPE), .in1(or_26_out), .out(BSel));  // open: gs, en_out, en_in
  and and_12 (R_xor, R_TYPE, comparator_20_eq, comparator_21_eq);
  and and_13 (R_srl, R_TYPE, comparator_22_eq, comparator_23_eq);
  and and_14 (R_sra, R_TYPE, comparator_24_eq, comparator_25_eq);
  and and_15 (R_or, R_TYPE, comparator_26_eq, comparator_27_eq);
  and and_16 (R_and, R_TYPE, comparator_28_eq, comparator_29_eq);
  Comparator #(.width(3)) comparator_30 (.a(Inst[14:12]), .b(3'b000), .eq(comparator_30_eq));  // open: gt, lt
  Comparator #(.width(7)) comparator_31 (.a(Inst[31:25]), .b({7{1'b0}}), .eq(comparator_31_eq));  // open: gt, lt
  Comparator #(.width(3)) comparator_32 (.a(Inst[14:12]), .b(3'b001), .eq(comparator_32_eq));  // open: gt, lt
  Comparator #(.width(7)) comparator_33 (.a(Inst[31:25]), .b({7{1'b0}}), .eq(comparator_33_eq));  // open: gt, lt
  Comparator #(.width(3)) comparator_34 (.a(Inst[14:12]), .b(3'b010), .eq(comparator_34_eq));  // open: gt, lt
  Comparator #(.width(7)) comparator_35 (.a(Inst[31:25]), .b({7{1'b0}}), .eq(comparator_35_eq));  // open: gt, lt
  Comparator #(.width(3)) comparator_36 (.a(Inst[14:12]), .b(3'b011), .eq(comparator_36_eq));  // open: gt, lt
  Comparator #(.width(7)) comparator_37 (.a(Inst[31:25]), .b({7{1'b0}}), .eq(comparator_37_eq));  // open: gt, lt
  Comparator #(.width(3)) comparator_38 (.a(Inst[14:12]), .b(3'b100), .eq(comparator_38_eq));  // open: gt, lt
  Comparator #(.width(7)) comparator_39 (.a(Inst[31:25]), .b({7{1'b0}}), .eq(comparator_39_eq));  // open: gt, lt
  and and_17 (I_add, I_TYPE, comparator_30_eq, comparator_31_eq);
  and and_18 (I_sll, I_TYPE, comparator_32_eq, comparator_33_eq);
  and and_19 (I_slt, I_TYPE, comparator_34_eq, comparator_35_eq);
  and and_20 (I_sltu, I_TYPE, comparator_36_eq, comparator_37_eq);
  and and_21 (I_xor, I_TYPE, comparator_38_eq, comparator_39_eq);
  Comparator #(.width(3)) comparator_40 (.a(Inst[14:12]), .b(3'b101), .eq(comparator_40_eq));  // open: gt, lt
  Comparator #(.width(7)) comparator_41 (.a(Inst[31:25]), .b({7{1'b0}}), .eq(comparator_41_eq));  // open: gt, lt
  Comparator #(.width(3)) comparator_42 (.a(Inst[14:12]), .b(3'b101), .eq(comparator_42_eq));  // open: gt, lt
  Comparator #(.width(7)) comparator_43 (.a(Inst[31:25]), .b(7'b0100000), .eq(comparator_43_eq));  // open: gt, lt
  Comparator #(.width(3)) comparator_44 (.a(Inst[14:12]), .b(3'b110), .eq(comparator_44_eq));  // open: gt, lt
  Comparator #(.width(7)) comparator_45 (.a(Inst[31:25]), .b({7{1'b0}}), .eq(comparator_45_eq));  // open: gt, lt
  Comparator #(.width(3)) comparator_46 (.a(Inst[14:12]), .b(3'b111), .eq(comparator_46_eq));  // open: gt, lt
  Comparator #(.width(7)) comparator_47 (.a(Inst[31:25]), .b({7{1'b0}}), .eq(comparator_47_eq));  // open: gt, lt
  and and_22 (I_srl, I_TYPE, comparator_40_eq, comparator_41_eq);
  and and_23 (I_sra, I_TYPE, comparator_42_eq, comparator_43_eq);
  and and_24 (I_or, I_TYPE, comparator_44_eq, comparator_45_eq);
  and and_25 (I_and, I_TYPE, comparator_46_eq, comparator_47_eq);
  Comparator #(.width(3)) comparator_48 (.a(Inst[14:12]), .b(3'b000), .eq(comparator_48_eq));  // open: gt, lt
  Comparator #(.width(3)) comparator_49 (.a(Inst[14:12]), .b(3'b001), .eq(comparator_49_eq));  // open: gt, lt
  Comparator #(.width(3)) comparator_50 (.a(Inst[14:12]), .b(3'b010), .eq(comparator_50_eq));  // open: gt, lt
  Comparator #(.width(3)) comparator_51 (.a(Inst[14:12]), .b(3'b100), .eq(comparator_51_eq));  // open: gt, lt
  Comparator #(.width(3)) comparator_52 (.a(Inst[14:12]), .b(3'b101), .eq(comparator_52_eq));  // open: gt, lt
  and and_26 (I_lb, I_TYPE_LOAD, comparator_48_eq);
  and and_27 (I_lh, I_TYPE_LOAD, comparator_49_eq);
  and and_28 (I_lw, I_TYPE_LOAD, comparator_50_eq);
  and and_29 (I_lbu, I_TYPE_LOAD, comparator_51_eq);
  and and_30 (I_lhu, I_TYPE_LOAD, comparator_52_eq);
  Comparator #(.width(3)) comparator_53 (.a(Inst[14:12]), .b(3'b010), .eq(comparator_53_eq));  // open: gt, lt
  Comparator #(.width(3)) comparator_54 (.a(Inst[14:12]), .b(3'b001), .eq(comparator_54_eq));  // open: gt, lt
  Comparator #(.width(3)) comparator_55 (.a(Inst[14:12]), .b(3'b000), .eq(comparator_55_eq));  // open: gt, lt
  Comparator #(.width(3)) comparator_56 (.a(Inst[14:12]), .b(3'b000), .eq(comparator_56_eq));  // open: gt, lt
  Comparator #(.width(3)) comparator_57 (.a(Inst[14:12]), .b(3'b001), .eq(comparator_57_eq));  // open: gt, lt
  Comparator #(.width(3)) comparator_58 (.a(Inst[14:12]), .b(3'b100), .eq(comparator_58_eq));  // open: gt, lt
  Comparator #(.width(3)) comparator_59 (.a(Inst[14:12]), .b(3'b101), .eq(comparator_59_eq));  // open: gt, lt
  Comparator #(.width(3)) comparator_60 (.a(Inst[14:12]), .b(3'b110), .eq(comparator_60_eq));  // open: gt, lt
  Comparator #(.width(3)) comparator_61 (.a(Inst[14:12]), .b(3'b111), .eq(comparator_61_eq));  // open: gt, lt
  and and_31 (S_sw, S_TYPE, comparator_53_eq);
  and and_32 (S_sh, S_TYPE, comparator_54_eq);
  and and_33 (S_sb, S_TYPE, comparator_55_eq);
  and and_34 (B_beq, B_TYPE, comparator_56_eq);
  and and_35 (B_bne, B_TYPE, comparator_57_eq);
  and and_36 (B_blt, B_TYPE, comparator_58_eq);
  and and_37 (B_bge, B_TYPE, comparator_59_eq);
  and and_38 (B_bltu, B_TYPE, comparator_60_eq);
  and and_39 (B_bgeu, B_TYPE, comparator_61_eq);

  assign out_3 = Inst[6:0];
  assign out_4 = Inst[11:7];
  assign out_5 = Inst[14:12];
  assign out_6 = Inst[19:15];
  assign out_7 = Inst[24:20];
  assign out_8 = Inst[31:25];

  // Other names for the same wires on the sheet: I_TYPE_JUMP = I_jalr; OPCODE[6:0] = Inst[6:0];
  //   IMM_4_0[4:0] = Inst[11:7]; IMM_11 = Inst[7]; RD[4:0] = Inst[11:7]; IMM_4_1[3:0] = Inst[11:8];
  //   FUNCT3[2:0] = Inst[14:12]; RS1[4:0] = Inst[19:15]; IMM_11_0[11:0] = Inst[31:20]; RS2[4:0] = Inst[24:20];
  //   FUNCT7[6:0] = Inst[31:25]; IMM_10_5[5:0] = Inst[30:25]; IMM_11_5[6:0] = Inst[31:25]; IMM_12 = Inst[31]

  // Notes on the sheet:
  //   EXECUTE
  //   ALU Operation Encoding
  //   PC MUX Selection
  //   INSTRUCTION DECODING
  //   R-TYPE
  //   I-TYPE
  //   WRITE BACK
  //   S-Type
  //   Memory Write Selection
endmodule

module Imm_Gen (
  input  [31:0] Inst,
  input  [2:0] ImmSel,
  output [31:0] Imm
);

  Multiplexer #(.select(3), .width(32), .enable("false")) multiplexer_1 (
    .in0({{21{Inst[31]}}, Inst[30:20]}), .in1({{21{Inst[31]}}, Inst[30:25], Inst[11:7]}),
    .in2({{20{Inst[31]}}, Inst[7], Inst[30:25], Inst[11:8], 1'b0}),
    .in3({{12{Inst[31]}}, Inst[19:12], Inst[20], Inst[30:21], 1'b0}), .in4({Inst[31:12], {12{1'b0}}}),
    .out(Imm), .sel(ImmSel));  // open: in5, in6, in7

  // Other names for the same wires on the sheet: FUNCT3[2:0] = Inst[14:12];
  //   J_TYPE[31:1] = {{12{Inst[31]}}, Inst[19:12], Inst[20], Inst[30:21]}; U_TYPE[31:12] = Inst[31:12];
  //   OPCODE[6:0] = Inst[6:0]; B_TYPE[31:1] = {{20{Inst[31]}}, Inst[7], Inst[30:25], Inst[11:8]};
  //   RD[4:0] = Inst[11:7]; S_TYPE[31:0] = {{21{Inst[31]}}, Inst[30:25], Inst[11:7]}; RS1[4:0] = Inst[19:15];
  //   I_TYPE[31:0] = {{21{Inst[31]}}, Inst[30:20]}; RS2[4:0] = Inst[24:20]; FUNCT7[6:0] = Inst[31:25]
endmodule

module Branch_Comp (
  input  [31:0] A,
  input  [31:0] B,
  input  [2:0] FUNCT3,
  output out_4
);

  wire comparator_1_eq, comparator_1_gt, comparator_1_lt, comparator_2_eq, comparator_2_gt, comparator_2_lt,
       demultiplexer_1_out0, demultiplexer_1_out1, demultiplexer_1_out4, demultiplexer_1_out5,
       demultiplexer_1_out6, demultiplexer_1_out7, multiplexer_1_out, multiplexer_2_out, multiplexer_3_out,
       multiplexer_4_out, not_1_out, or_1_out, or_2_out;

  Comparator #(.width(32)) comparator_1 (
    .a(A), .b(B), .gt(comparator_1_gt), .eq(comparator_1_eq), .lt(comparator_1_lt));
  Comparator #(.width(32), .mode("unsigned")) comparator_2 (
    .a(A), .b(B), .gt(comparator_2_gt), .eq(comparator_2_eq), .lt(comparator_2_lt));
  or or_1 (or_1_out, comparator_1_gt, comparator_1_eq);
  or or_2 (or_2_out, comparator_2_gt, comparator_2_eq);
  Multiplexer multiplexer_1 (
    .in0(or_1_out), .in1(comparator_1_eq), .out(multiplexer_1_out), .sel(demultiplexer_1_out0));  // open: en
  Multiplexer multiplexer_2 (
    .in0(multiplexer_1_out), .in1(not_1_out), .out(multiplexer_2_out), .sel(demultiplexer_1_out1));  // open: en
  not not_1 (not_1_out, comparator_1_eq);
  Demultiplexer #(.select(3), .enable("false")) demultiplexer_1 (
    .out0(demultiplexer_1_out0), .out1(demultiplexer_1_out1), .out4(demultiplexer_1_out4),
    .out5(demultiplexer_1_out5), .out6(demultiplexer_1_out6), .out7(demultiplexer_1_out7), .in(1'b1),
    .sel(FUNCT3));  // open: out2, out3
  Multiplexer multiplexer_3 (
    .in0(multiplexer_2_out), .in1(comparator_1_lt), .out(multiplexer_3_out), .sel(demultiplexer_1_out4));  // open: en
  Multiplexer multiplexer_4 (
    .in0(multiplexer_3_out), .in1(or_2_out), .out(multiplexer_4_out), .sel(demultiplexer_1_out7));  // open: en
  Multiplexer multiplexer_5 (
    .in0(multiplexer_4_out), .in1(comparator_2_lt), .out(out_4), .sel(demultiplexer_1_out6));  // open: en

  // Notes on the sheet:
  //   unsigned
  //   beq
  //   bge
  //   bne
  //   blt
  //   bgeu
  //   bltu
endmodule

module MEM_WB (
  input  RegWEn,
  input  [1:0] WBSel,
  input  CLK,
  output RegWEnout,
  output [1:0] WBSELout
);

  Register #(.width(1)) register_1 (.D(RegWEn), .en(CLK), .Q(RegWEnout));  // open: clk, clr
  Register #(.width(2)) register_2 (.D(WBSel), .clk(CLK), .Q(WBSELout));  // open: en, clr

  // Notes on the sheet:
  //   WB
endmodule

module EX_MEM (
  input  RegWEn,
  input  [1:0] WBSel,
  input  MemRW,
  input  PCSel,
  input  CLK,
  output RegWEnout,
  output [1:0] WBSelout,
  output MemRWout,
  output PCSelout
);

  Register #(.width(1)) register_1 (.D(RegWEn), .en(CLK), .Q(RegWEnout));  // open: clk, clr
  Register #(.width(2)) register_2 (.D(WBSel), .clk(CLK), .Q(WBSelout));  // open: en, clr
  Register #(.width(1)) register_3 (.D(MemRW), .en(CLK), .Q(MemRWout));  // open: clk, clr
  Register #(.width(1)) register_4 (.D(PCSel), .en(CLK), .Q(PCSelout));  // open: clk, clr

  // Notes on the sheet:
  //   WB
  //   MEM
endmodule

module ID_EX (
  input  RegWEn,
  input  [1:0] WBSel,
  input  MemRW,
  input  PCSel,
  input  ASel,
  input  BSel,
  input  [3:0] ALUSel,
  input  [2:0] ImmSel,
  input  [2:0] Funct3,
  input  CLK,
  output RegWEnout,
  output [1:0] WBSelout,
  output MemRWout,
  output PCSelout,
  output ASelout,
  output BSelout,
  output [3:0] ALUSelout,
  output [2:0] ImmSelout,
  output [2:0] Funct3out
);

  Register #(.width(1)) register_1 (.D(RegWEn), .en(CLK), .Q(RegWEnout));  // open: clk, clr
  Register #(.width(2)) register_2 (.D(WBSel), .clk(CLK), .Q(WBSelout));  // open: en, clr
  Register #(.width(1)) register_3 (.D(MemRW), .en(CLK), .Q(MemRWout));  // open: clk, clr
  Register #(.width(1)) register_4 (.D(PCSel), .en(CLK), .Q(PCSelout));  // open: clk, clr
  Register #(.width(1)) register_5 (.D(ASel), .en(CLK), .Q(ASelout));  // open: clk, clr
  Register #(.width(1)) register_6 (.D(BSel), .clk(CLK), .Q(BSelout));  // open: en, clr
  Register #(.width(4)) register_7 (.D(ALUSel), .clk(CLK), .Q(ALUSelout));  // open: en, clr
  Register #(.width(3)) register_8 (.D(ImmSel), .clk(CLK), .Q(ImmSelout));  // open: en, clr
  Register #(.width(3)) register_9 (.D(Funct3), .clk(CLK), .Q(Funct3out));  // open: en, clr

  // Notes on the sheet:
  //   WB
  //   MEM
  //   EX
endmodule

module FWRD_LOGIC (
  input  [31:0] RS1,
  input  [31:0] RS2,
  input  [31:0] RS2Mem,
  input  [31:0] MemWB,
  output [1:0] ASel,
  output [1:0] Bsel
);

  wire comparator_1_eq, comparator_2_eq, comparator_3_eq, comparator_4_eq;

  Comparator #(.width(32), .mode("unsigned")) comparator_1 (.a(RS1), .b(RS2Mem), .eq(comparator_1_eq));  // open: gt, lt
  Comparator #(.width(32), .mode("unsigned")) comparator_2 (.a(RS2), .b(RS2Mem), .eq(comparator_2_eq));  // open: gt, lt
  Comparator #(.width(32), .mode("unsigned")) comparator_3 (.a(RS1), .b(MemWB), .eq(comparator_3_eq));  // open: gt, lt
  Comparator #(.width(32), .mode("unsigned")) comparator_4 (.a(RS2), .b(MemWB), .eq(comparator_4_eq));  // open: gt, lt
endmodule
