// Logisim project JK_Flip_Flop.circ as structural Verilog: 1 circuit, main circuit main
module main (
  input  in_1,
  input  in_2,
  output Q,
  output QBar,
  output out_5,
  output out_6,
  output out_7,
  output out_8,
  output out_9,
  output out_10
);

  wire and_1_out, and_2_out, CLK, j_k_ff_2_qn, j_k_ff_3_qn, j_k_ff_4_qn;

  Clock clock_1 (.out(CLK));
  J_K_Flip_Flop j_k_ff_1 (.J(1'b1), .K(1'b1), .clk(j_k_ff_2_qn), .Q(out_7));  // open: Qn, preset, reset
  J_K_Flip_Flop j_k_ff_2 (.J(1'b1), .K(1'b1), .clk(j_k_ff_3_qn), .Q(out_8), .Qn(j_k_ff_2_qn));  // open: preset, reset
  and and_1 (and_1_out, QBar, in_1, CLK);
  and and_2 (and_2_out, CLK, in_2, Q);
  J_K_Flip_Flop j_k_ff_3 (.J(1'b1), .K(1'b1), .clk(j_k_ff_4_qn), .Q(out_9), .Qn(j_k_ff_3_qn));  // open: preset, reset
  J_K_Flip_Flop j_k_ff_4 (.J(1'b1), .K(1'b1), .clk(CLK), .Q(out_10), .Qn(j_k_ff_4_qn));  // open: preset, reset
  nor nor_1 (Q, and_1_out, QBar);
  nor nor_2 (QBar, Q, and_2_out);
  J_K_Flip_Flop j_k_ff_5 (.J(in_1), .K(in_2), .clk(CLK), .Q(out_5), .Qn(out_6));  // open: preset, reset

  // Other names for the same wires on the sheet: J = in_1; K = in_2

  // Notes on the sheet:
  //   Binary Counter
  //   J-K-Flip Flop
endmodule
