// Logisim project accumulator.circ as structural Verilog: 2 circuits, main circuit AddMachine
module AddMachine (
  output [7:0] ADD_OUT,
  output [7:0] REG_OUT
);

  wire clock_1_out;

  Clock clock_1 (.out(clock_1_out));
  Adder adder_1 (.a(8'h1), .b(REG_OUT), .out(ADD_OUT));  // open: cin, cout
  Register register_1 (.D(ADD_OUT), .clk(clock_1_out), .Q(REG_OUT));  // open: en, clr

  // Notes on the sheet:
  //   Accumulator
endmodule

module FSM (
  input  [7:0] CIRCUIT_INPUT,
  output [7:0] CIRCUIT_OUTPUT,
  output [7:0] NEXT_STATE,
  output [7:0] PRESENT_STATE
);

  wire clock_1_out;

  Clock clock_1 (.out(clock_1_out));
  Adder adder_1 (.a(CIRCUIT_INPUT), .b(PRESENT_STATE), .out(CIRCUIT_OUTPUT));  // open: cin, cout
  Register register_1 (.D(CIRCUIT_OUTPUT), .clk(clock_1_out), .Q(PRESENT_STATE));  // open: en, clr

  assign NEXT_STATE = CIRCUIT_OUTPUT;

  // Notes on the sheet:
  //   FSM JUST FOR VISUALIZATION
  //   SOME COMBINATION LOGIC
endmodule
