// Logisim project alu.circ as structural Verilog: 8 circuits, main circuit main
module main (
  input  [15:0] X,
  input  [15:0] Y,
  input  [3:0] Switch_S_b4f65fa4,
  output Signed_Overflow_2abdd9f8,
  output [15:0] RESULT,
  output Equal
);

  wire a8Spill, addSpill, s8Spill, subSpill;
  wire [15:0] addof_1_out, addp8_1_out, and_1_out, or_1_out, shifter_1_out, shifter_2_out, shifter_3_out,
       slt_1_out, subof_1_out, subp8_1_out;

  addOF addof_1 (.in_1(X), .in_2(Y), .out_2(addSpill), .out(addof_1_out));
  subOF subof_1 (.in_1(X), .in_2(Y), .out_2(subSpill), .out(subof_1_out));
  Shifter #(.width(16)) shifter_1 (.in(X), .\dist (Y[3:0]), .out(shifter_1_out));
  Shifter #(.width(16), .shift("lr")) shifter_2 (.in(X), .\dist (Y[3:0]), .out(shifter_2_out));
  Shifter #(.width(16), .shift("ar")) shifter_3 (.in(X), .\dist (Y[3:0]), .out(shifter_3_out));
  slt slt_1 (.in_1(X), .in_2(Y), .out(slt_1_out));
  assign or_1_out = X | Y;  // OR_Gate or_1, 16 bits wide
  assign and_1_out = X & Y;  // AND_Gate and_1, 16 bits wide
  addp8 addp8_1 (.in_1(X), .in_2(Y), .out_2(a8Spill), .out(addp8_1_out));
  subp8 subp8_1 (.in_1(X), .in_2(Y), .out_2(s8Spill), .out(subp8_1_out));
  Multiplexer #(.select(4), .width(16)) multiplexer_1 (
    .in0(addof_1_out), .in1(subof_1_out), .in2(shifter_1_out), .in3(shifter_2_out), .in4(shifter_3_out),
    .in5(slt_1_out), .in6(or_1_out), .in7(and_1_out), .in8(addp8_1_out), .in9(subp8_1_out), .out(RESULT),
    .sel(Switch_S_b4f65fa4));  // open: in10, in11, in12, in13, in14, in15, en
  Multiplexer #(.select(4)) multiplexer_2 (
    .in0(addSpill), .in1(subSpill), .in2(1'b0), .in3(1'b0), .in4(1'b0), .in5(1'b0), .in6(1'b0), .in7(1'b0),
    .in8(a8Spill), .in9(s8Spill), .in10(1'b0), .in11(1'b0), .in12(1'b0), .in13(1'b0), .in14(1'b0),
    .in15(1'b0), .out(Signed_Overflow_2abdd9f8), .sel(Switch_S_b4f65fa4));  // open: en
  Comparator #(.width(16)) comparator_1 (.a(X), .b(Y), .eq(Equal));  // open: gt, lt

  // Other names for the same wires on the sheet: Y4[3:0] = Y[3:0]

  // Notes on the sheet:
  //   INPUTS to your circuit
  //   INPUT to your circuit
  //   DON'T CHANGE THE INPUTS AND OUTPUTS! IF YOU DO SO, YOU NEED TO MAKE SURE THE PINS ARE IN THE RIGHT PLACES!
  //   OUTPUTS of your circuit
endmodule

module slt (
  input  [15:0] in_1,
  input  [15:0] in_2,
  output [15:0] out
);

  wire comparator_1_lt;

  // Probe on in_1
  // Probe on in_2
  Comparator #(.width(16)) comparator_1 (.a(in_1), .b(in_2), .lt(comparator_1_lt));  // open: gt, eq
  Multiplexer #(.width(16)) multiplexer_1 (
    .in0({16{1'b0}}), .in1(16'h1), .out(out), .sel(comparator_1_lt));  // open: en
endmodule

module addp8 (
  input  [15:0] in_1,
  input  [15:0] in_2,
  output [15:0] out,
  output out_2
);

  wire add8_1_out_2, add8_2_out_2;

  add8 add8_1 (.in_1(in_1[7:0]), .in_2(in_2[7:0]), .out_2(add8_1_out_2), .out(out[7:0]));
  add8 add8_2 (.in_1(in_1[15:8]), .in_2(in_2[15:8]), .out_2(add8_2_out_2), .out(out[15:8]));
  or or_1 (out_2, add8_2_out_2, add8_1_out_2);
endmodule

module sub8 (
  input  [7:0] in_1,
  input  [7:0] in_2,
  output [7:0] out,
  output out_2
);

  wire and_1_out, and_2_out, not_1_out, not_2_out, not_3_out;

  and and_1 (and_1_out, in_1[7], not_1_out, not_3_out);
  not not_1 (not_1_out, in_2[7]);
  and and_2 (and_2_out, in_2[7], not_2_out, out[7]);
  or or_1 (out_2, and_1_out, and_2_out);
  not not_2 (not_2_out, in_1[7]);
  not not_3 (not_3_out, out[7]);
  Subtractor subtractor_1 (.a(in_1), .b(in_2), .out(out));  // open: bin, bout
endmodule

module addOF (
  input  [15:0] in_1,
  input  [15:0] in_2,
  output [15:0] out,
  output out_2
);

  wire and_1_out, and_2_out, not_1_out, not_2_out, not_3_out;

  not not_1 (not_1_out, in_1[15]);
  Adder #(.width(16)) adder_1 (.a(in_1), .b(in_2), .out(out));  // open: cin, cout
  not not_2 (not_2_out, in_2[15]);
  not not_3 (not_3_out, out[15]);
  and and_1 (and_1_out, not_1_out, out[15], not_2_out);
  and and_2 (and_2_out, in_2[15], not_3_out, in_1[15]);
  or or_1 (out_2, and_2_out, and_1_out);
endmodule

module subOF (
  input  [15:0] in_1,
  input  [15:0] in_2,
  output [15:0] out,
  output out_2
);

  wire and_1_out, and_2_out, not_1_out, not_2_out, not_3_out;

  and and_1 (and_1_out, in_1[15], not_2_out, not_3_out);
  not not_1 (not_1_out, in_1[15]);
  not not_2 (not_2_out, in_2[15]);
  and and_2 (and_2_out, in_2[15], not_1_out, out[15]);
  or or_1 (out_2, and_1_out, and_2_out);
  Subtractor #(.width(16)) subtractor_1 (.a(in_1), .b(in_2), .out(out));  // open: bin, bout
  not not_3 (not_3_out, out[15]);
endmodule

module add8 (
  input  [7:0] in_1,
  input  [7:0] in_2,
  output [7:0] out,
  output out_2
);

  wire and_1_out, and_2_out, not_1_out, not_2_out, not_3_out;

  not not_1 (not_1_out, in_1[7]);
  not not_2 (not_2_out, in_2[7]);
  and and_1 (and_1_out, not_1_out, not_2_out, out[7]);
  or or_1 (out_2, and_1_out, and_2_out);
  Adder adder_1 (.a(in_1), .b(in_2), .out(out));  // open: cin, cout
  and and_2 (and_2_out, in_1[7], in_2[7], not_3_out);
  not not_3 (not_3_out, out[7]);
endmodule

module subp8 (
  input  [15:0] in_1,
  input  [15:0] in_2,
  output [15:0] out,
  output out_2
);

  wire sub8_1_out_2, sub8_2_out_2;

  sub8 sub8_1 (.in_1(in_1[7:0]), .in_2(in_2[7:0]), .out_2(sub8_1_out_2), .out(out[7:0]));
  sub8 sub8_2 (.in_1(in_1[15:8]), .in_2(in_2[15:8]), .out_2(sub8_2_out_2), .out(out[15:8]));
  or or_1 (out_2, sub8_2_out_2, sub8_1_out_2);
endmodule
