// Logisim project UnsignedMultAttempt.circ as structural Verilog: 1 circuit, main circuit main
module main (
  input  [3:0] in_1,
  input  [3:0] in_2,
  input  control,
  input  in_4,
  output [3:0] out_5,
  output [3:0] out_6,
  output [7:0] out_7
);

  wire CLK;
  wire [3:0] AC_q, MD_q, MQ_q;

  Clock clock_1 (.out(CLK));
  Register #(.width(4)) MD (.D(in_1), .clk(CLK), .Q(MD_q));  // open: en, clr
  Multiplexer #(.width(4), .enable("false")) multiplexer_1 (.in0(4'b0000), .in1(MD_q), .out(out_5), .sel(control));
  Adder #(.width(4)) adder_1 (.a(out_5), .b(AC_q), .out(out_6));  // open: cin, cout
  Register #(.width(4)) AC (.D(out_6), .clk(CLK), .Q(AC_q), .clr(in_4));  // open: en
  Register #(.width(4)) MQ (.D(in_2), .clk(CLK), .Q(MQ_q));  // open: en, clr
  Multiplier multiplier_1 ();  // open: a, b, out, cin, cout
  Register ACplusMQ (.D({{2{AC_q[3]}}, AC_q[2:0], MQ_q[3:1]}), .clk(CLK), .Q(out_7));  // open: en, clr

  // Other names for the same wires on the sheet: MD[3:0] = in_1; MQ[3:0] = in_2

  // Notes on the sheet:
  //   MD = multiplicand (n bit)
  //   MQ = multiplier (n bit)
  //   AC = accumulator (n bit)
  //   AC:MQ = product (2n bit)
endmodule
