// Logisim project directMapped.circ as structural Verilog: 1 circuit, main circuit main
module main (
  input  [31:0] in_1,
  output [1:0] out_2,
  output [9:0] out_3,
  output [19:0] out_4
);


  assign out_2 = in_1[1:0];
  assign out_3 = in_1[11:2];
  assign out_4 = in_1[31:12];

  // Other names for the same wires on the sheet: BlockOffset[1:0] = in_1[1:0]; Index[9:0] = in_1[11:2];
  //   Tag[19:0] = in_1[31:12]
endmodule
