// Logisim project combining_circuits.circ as structural Verilog: 2 circuits, main circuit main
module main (
  input  in_1,
  input  in_2,
  output out_3,
  output out_4,
  output out_5
);

  test test_1 (.a(in_1), .b(in_2), .aloha(out_3));
  test test_2 (.a(out_3), .b(in_1), .aloha(out_4));
  test test_3 (.a(in_1), .b(in_1), .aloha(out_5));
endmodule

module test (
  input  a,
  input  b,
  output aloha
);

  and and_1 (aloha, a, b);
endmodule
