// Logisim project edge_detectors.circ as structural Verilog: 1 circuit, main circuit main
module main (
  output out_1
);

  wire CLK, not_1_out;

  Clock clock_1 (.out(CLK));
  not not_1 (not_1_out, CLK);
  and and_1 (out_1, CLK, not_1_out);

  // Notes on the sheet:
  //   Rising-Edge Detector
endmodule
