// Logisim project full_adder.circ as structural Verilog: 1 circuit, main circuit main
module main (
  input  in_1,
  input  in_2,
  input  in_3,
  output out_4,
  output out_5,
  output out_6,
  output out_7,
  output out_8,
  output out_9
);

  wire and_1_out, and_2_out, nand_1_out, nand_2_out, nand_3_out, nand_4_out, nand_5_out, nand_6_out,
       nand_7_out, nand_9_out, nand_10_out, nand_11_out, nand_12_out, nand_13_out, nand_14_out, xor_1_out;

  Adder #(.width(1)) adder_1 (.a(in_1), .b(in_2), .out(out_4), .cin(in_3), .cout(out_5));
  xor xor_1 (xor_1_out, in_1, in_2);
  xor xor_2 (out_7, xor_1_out, in_3);
  and and_1 (and_1_out, in_3, xor_1_out);
  and and_2 (and_2_out, in_2, in_1);
  or or_1 (out_8, and_1_out, and_2_out);
  nand nand_1 (nand_1_out, in_1, in_2);
  nand nand_2 (nand_2_out, in_1, nand_1_out);
  nand nand_3 (nand_3_out, nand_1_out, in_2);
  nand nand_4 (nand_4_out, nand_2_out, nand_3_out);
  nand nand_5 (nand_5_out, nand_4_out, in_3);
  nand nand_6 (nand_6_out, nand_4_out, nand_5_out);
  nand nand_7 (nand_7_out, nand_5_out, in_3);
  nand nand_8 (out_6, nand_6_out, nand_7_out);
  nand nand_9 (nand_9_out, in_3, nand_4_out);
  nand nand_10 (nand_10_out, in_2, in_1);
  nand nand_11 (nand_11_out, nand_9_out, nand_9_out);
  nand nand_12 (nand_12_out, nand_10_out, nand_10_out);
  nand nand_13 (nand_13_out, nand_11_out, nand_11_out);
  nand nand_14 (nand_14_out, nand_12_out, nand_12_out);
  nand nand_15 (out_9, nand_13_out, nand_14_out);

  // Other names for the same wires on the sheet: a = in_1; b = in_2; cin = in_3

  // Notes on the sheet:
  //   Full Adder
  //   Adder represented with logic gates
  //   not implemented here
  //   IT IS POSSIBLE TO MAKE A FULL ADDER WITH ONLY 9 NAND GATES!
  //   adder gates broken down with NAND gates
  //   NOTE:HALF ADDER DOES NOT HAVE CIN
endmodule
