// Logisim project majority_gate_ADDER_logic.circ as structural Verilog: 1 circuit, main circuit main
module main (
  input  in_1,
  input  in_2,
  input  in_3,
  input  in_4,
  input  in_5,
  input  in_6,
  input  in_7,
  input  in_8,
  input  SUB,
  output out_10,
  output out_11,
  output si,
  output y,
  output Number,
  output Sign,
  output SIGNOVFLW,
  output s1,
  output UNSIGNOVFLW,
  output s2,
  output Ci_plus1_or_y_comparedabove
);

  wire adder_3_cout, adder_4_cout, adder_5_cout, and_1_out, and_2_out, and_3_out, xor_2_out, xor_3_out;

  Adder #(.width(1)) adder_1 (.a(in_2), .b(in_3), .cin(in_8), .cout(out_10));  // open: out
  Adder #(.width(1)) adder_2 (.a(in_4), .b(in_5), .cin(out_10), .cout(Ci_plus1_or_y_comparedabove));  // open: out
  and and_1 (and_1_out, in_1, in_6);
  and and_2 (and_2_out, in_6, in_7);
  and and_3 (and_3_out, in_7, in_1);
  or or_1 (y, and_1_out, and_2_out, and_3_out);
  Adder #(.width(1)) adder_3 (.a(in_2), .b(in_3), .out(s1), .cin(in_8), .cout(adder_3_cout));
  Adder #(.width(1)) adder_4 (.a(in_4), .b(in_5), .out(s2), .cin(adder_3_cout), .cout(adder_4_cout));
  ExactlyOne xor_1 (.out(si), .in0(in_1), .in1(in_6), .in2(in_7));
  xor xor_2 (xor_2_out, SUB, in_3);
  xor xor_3 (xor_3_out, SUB, in_5);
  Adder #(.width(1)) adder_5 (.a(in_2), .b(xor_2_out), .out(Number), .cin(SUB), .cout(adder_5_cout));
  Adder #(.width(1)) adder_6 (.a(in_4), .b(xor_3_out), .out(Sign), .cin(adder_5_cout), .cout(UNSIGNOVFLW));
  xor xor_4 (SIGNOVFLW, adder_5_cout, UNSIGNOVFLW);

  assign out_11 = Ci_plus1_or_y_comparedabove;

  // Other names for the same wires on the sheet: A_0 = in_2; A_1 = in_4; Ai = in_1; B_0 = in_3; B_1 = in_5; Bi = in_6;
  //   CIN_0 = in_8; CIN_1 = out_10; CIN_2 = Ci_plus1_or_y_comparedabove; CINi = in_7

  // Notes on the sheet:
  //   MAJORITY, USED TO OBTAIN THE CARRY-IN OUTPUT ON AN ADDER IE Ci+1
  //   Ci+1
  //   Ci+1
  //   COMBINING THESE LOGICS WE CAN MAKE  A FULL ADDER, SEE FULL ADDER CIRCUIT
  //   Ci+1
  //   XOR, USED TO OBTAIN SI
  //   SUBTRACTOR DESIGN
  //   SUB = 0, ADDITION
  //   SUB = 1. SUBTRAC
endmodule
