// Logisim project memory_tests.circ as structural Verilog: 1 circuit, main circuit main
module main (
  input  [31:0] in_1,
  input  in_2,
  input  in_3,
  input  [31:0] in_4,
  output [31:0] out_5
);

  RAM #(.addrWidth(24), .dataWidth(32), .trigger("falling"), .databus("bibus")) ram_1 (
    .addr(in_1[25:2]), .we(in_2), .oe(1'b1), .clk(in_3), .din(in_4), .dout(out_5));

  // Notes on the sheet:
  //   RAM
endmodule
