// Logisim project mux.circ as structural Verilog: 1 circuit, main circuit main
module main (
  input  A,
  input  B,
  input  S,
  output out_4,
  output out_5
);

  wire and_1_out, and_2_out, not_1_out;

  not not_1 (not_1_out, S);
  and and_1 (and_1_out, not_1_out, A);
  and and_2 (and_2_out, S, B);
  or or_1 (out_4, and_1_out, and_2_out);
  Multiplexer #(.enable("false")) multiplexer_1 (.in0(A), .in1(B), .out(out_5), .sel(S));

  // Other names for the same wires on the sheet: Sel = S

  // Notes on the sheet:
  //   Mux = SbarA+SB
endmodule
