// Logisim project simple_alu.circ as structural Verilog: 1 circuit, main circuit main
module main (
  input  [31:0] A,
  input  [31:0] B,
  input  S0,
  input  S1,
  output [31:0] R,
  output UNSIGNEDOVERFLOW
);

  wire [31:0] adder_1_out, and_1_out, multiplexer_1_out, or_1_out;

  Adder #(.width(32)) adder_1 (.a(B), .b(A), .out(adder_1_out), .cin(S0), .cout(UNSIGNEDOVERFLOW));
  assign and_1_out = A & B;  // AND_Gate and_1, 32 bits wide
  Multiplexer #(.width(32), .enable("false")) multiplexer_1 (
    .in0(and_1_out), .in1(or_1_out), .out(multiplexer_1_out), .sel(S0));
  Multiplexer #(.width(32), .enable("false")) multiplexer_2 (
    .in0(adder_1_out), .in1(multiplexer_1_out), .out(R), .sel(S1));
  assign or_1_out = A | B;  // OR_Gate or_1, 32 bits wide

  // Notes on the sheet:
  //   SIMPLE ALU
endmodule
