// Logisim project simple_alu2.circ as structural Verilog: 1 circuit, main circuit main
module main (
  input  in_1,
  input  [31:0] in_2,
  input  [31:0] in_3,
  input  S0,
  input  S1,
  output [31:0] out_6,
  output [31:0] out_7,
  output [31:0] out_8,
  output [31:0] out_9,
  output SIGNEDOVERFLOW,
  output UNSIGNEDOVERFLOW
);

  wire adder_1_cout, not_2_out, xnor_1_out, xor_1_out;
  wire [31:0] adder_1_out, and_3_out, multiplexer_1_out, multiplexer_2_out, not_1_out, or_1_out;

  NotExactlyOne xnor_1 (.out(xnor_1_out), .in0(in_1), .in1(in_2[31]), .in2(in_3[31]));
  xor xor_1 (xor_1_out, in_2[31], adder_1_out[31]);
  and and_1 (SIGNEDOVERFLOW, xnor_1_out, xor_1_out, not_2_out);
  assign not_1_out = ~in_3;  // NOT_Gate not_1, 32 bits wide
  Multiplexer #(.width(32), .enable("false")) multiplexer_1 (
    .in0(in_3), .in1(not_1_out), .out(multiplexer_1_out), .sel(in_1));
  not not_2 (not_2_out, in_1);
  and and_2 (UNSIGNEDOVERFLOW, not_2_out, adder_1_cout);
  Adder #(.width(32)) adder_1 (.a(multiplexer_1_out), .b(in_2), .out(adder_1_out), .cin(in_1), .cout(adder_1_cout));
  assign and_3_out = in_2 & in_3;  // AND_Gate and_3, 32 bits wide
  Multiplexer #(.width(32), .enable("false")) multiplexer_2 (
    .in0(and_3_out), .in1(or_1_out), .out(multiplexer_2_out), .sel(S0));
  Multiplexer #(.width(32), .enable("false")) multiplexer_3 (
    .in0(adder_1_out), .in1(multiplexer_2_out), .out(out_8), .sel(S1));
  assign or_1_out = in_2 | in_3;  // OR_Gate or_1, 32 bits wide

  assign out_6 = in_2;
  assign out_7 = in_3;
  assign out_9 = out_8;

  // Other names for the same wires on the sheet: A[31:0] = in_2; B[31:0] = in_3; RESULT[31:0] = out_8; SUB = in_1

  // Notes on the sheet:
  //   SIMPLE ALU 2
endmodule
