// Logisim project test_register.circ as structural Verilog: 1 circuit, main circuit main
module main (
  input  [7:0] DATA,
  input  in_2,
  input  in_3,
  input  DATA_2,
  output [7:0] Q_OUTPUT,
  output Q_OUT
);

  wire CLK;

  Clock clock_1 (.out(CLK));
  Register register_1 (.D(DATA), .en(in_2), .clk(CLK), .Q(Q_OUTPUT), .clr(in_3));
  D_Flip_Flop D_FLIP_FLOP (.D(DATA_2), .clk(CLK), .Q(Q_OUT), .reset(in_3));  // open: Qn, preset

  // Other names for the same wires on the sheet: RESET = in_3; WRITE_ENABLE = in_2
endmodule
