// Logisim project test_tunnel.circ as structural Verilog: 1 circuit, main circuit main
module main (
  input  [7:0] in_1,
  input  [7:0] in_2,
  output [7:0] out_3,
  output [7:0] out_4,
  output [7:0] out_5
);


  assign out_3 = in_1;
  assign out_4 = in_1;
  assign out_5 = in_2;

  // Other names for the same wires on the sheet: x[7:0] = in_1; y[7:0] = in_2
endmodule
