// Logisim project universal_gate.circ as structural Verilog: 1 circuit, main circuit main
module main (
  input  in_1,
  input  in_2,
  input  in_3,
  input  in_4,
  input  in_5,
  input  in_6,
  input  in_7,
  input  in_8,
  input  in_9,
  input  in_10,
  input  in_11,
  output out_12,
  output out_13,
  output out_14,
  output out_15,
  output out_16,
  output out_17,
  output out_18,
  output out_19,
  output out_20,
  output out_21,
  output out_22
);

  wire nand_2_out, nand_3_out, nand_4_out, nand_8_out, nand_9_out, nand_10_out, nand_11_out, nand_12_out,
       nand_13_out, nand_15_out;

  nand nand_1 (out_13, in_4, in_4);
  nand nand_2 (nand_2_out, in_5, in_7);
  nand nand_3 (nand_3_out, in_8, in_8);
  nand nand_4 (nand_4_out, in_10, in_10);
  nand nand_5 (out_17, nand_2_out, nand_2_out);
  nand nand_6 (out_19, nand_3_out, nand_4_out);
  not not_1 (out_14, in_4);
  and and_1 (out_18, in_5, in_7);
  or or_1 (out_20, in_8, in_10);
  nand nand_7 (out_12, in_1, in_2);
  nand nand_8 (nand_8_out, in_3, in_6);
  nand nand_9 (nand_9_out, in_9, in_11);
  nand nand_10 (nand_10_out, in_3, nand_8_out);
  nand nand_11 (nand_11_out, nand_8_out, in_6);
  nand nand_12 (nand_12_out, in_9, nand_9_out);
  nand nand_13 (nand_13_out, nand_9_out, in_11);
  nand nand_14 (out_15, nand_10_out, nand_11_out);
  nand nand_15 (nand_15_out, nand_12_out, nand_13_out);
  nand nand_16 (out_21, nand_15_out, nand_15_out);
  xor xor_1 (out_16, in_3, in_6);
  xnor xnor_1 (out_22, in_9, in_11);

  // Notes on the sheet:
  //   NOT GATE
  //   AND GATE
  //   OR GATE
  //   NAND GATE THE UNIVERSAL GATE
  //   using NAND to build gates, corresponding gate attached at the end
  //   XOR GATE
  //   XNOR GATE
endmodule
