// Logisim project RV32I_v4ext_Stype_mem_visual.circ as structural Verilog: 7 circuits, main circuit main
module main (
  input  in_1,
  output [6:0] out_2,
  output [4:0] out_3,
  output [2:0] out_4,
  output [4:0] out_5,
  output [6:0] out_6,
  output [31:0] out_7,
  output [4:0] out_8,
  output [31:0] out_9,
  output [31:0] out_10,
  output [31:0] out_11,
  output [31:0] out_12
);

  wire BSel, CLK, ImmSel, MemRW, not_1_out, RegWEn, WBSel;
  wire [3:0] ALUSel;
  wire [9:0] register_1_q;
  wire [31:0] adder_1_out, INSTRUCTION, multiplexer_1_out, regfile_1_dataa;
  wire [31:10] register_1_q_2;

  Register #(.width(32)) register_1 (
    .D(adder_1_out), .clk(CLK), .Q({register_1_q_2, register_1_q}), .clr(in_1));  // open: en
  ROM #(.addrWidth(10), .dataWidth(32)) rom_1 (.addr(register_1_q), .data(INSTRUCTION));
  Adder #(.width(32)) adder_1 (.a(32'h1), .b({register_1_q_2, register_1_q}), .out(adder_1_out));  // open: cin, cout
  Imm_Gen imm_gen_1 (.Inst(INSTRUCTION), .ImmSel(ImmSel), .Imm(out_12));
  RegFile regfile_1 (
    .DataD(out_10), .AddrD(INSTRUCTION[11:7]), .AddrA(INSTRUCTION[19:15]), .AddrB(INSTRUCTION[24:20]),
    .in_5(RegWEn), .in_6(CLK), .DataA(regfile_1_dataa), .DataB(out_9));
  Multiplexer #(.width(32), .enable("false")) multiplexer_1 (
    .in0(out_9), .in1(out_12), .out(multiplexer_1_out), .sel(BSel));
  Clock clock_1 (.out(CLK));
  CONTROL_LOGIC control_logic_1 (
    .Inst(INSTRUCTION), .out_2(out_2), .out_3(out_3), .out_4(out_4), .out_5(out_5), .out_6(out_8),
    .out_7(out_6), .RegWEn(RegWEn), .BSel(BSel), .ImmSel(ImmSel), .ALUSel(ALUSel), .WBSel(WBSel),
    .MemRW(MemRW));
  ALU alu_1 (.rs1(regfile_1_dataa), .rs2(multiplexer_1_out), .OP(ALUSel), .R(out_7));
  Multiplexer #(.width(32), .enable("false")) multiplexer_2 (.in0(out_11), .in1(out_7), .out(out_10), .sel(WBSel));
  not not_1 (not_1_out, MemRW);
  RAM #(.addrWidth(10), .dataWidth(32), .databus("bibus")) ram_1 (
    .addr(out_7[9:0]), .we(MemRW), .oe(not_1_out), .clk(CLK), .din(out_9), .dout(out_11));

  // Other names for the same wires on the sheet: ALU_Out[31:0] = out_7; FINAL_OUTPUT[31:0] = out_10;
  //   FUNCT3[2:0] = out_4; FUNCT7[6:0] = out_6; Mem_In[31:0] = out_9; Mem_offset[31:0] = out_12;
  //   Memory_Out[31:0] = out_11; OPCODE[6:0] = out_2; RD[4:0] = out_3; RS1[4:0] = out_5; RS2[4:0] = out_8

  // Notes on the sheet:
  //   contents of rom_1 (hex, n*v repeats v):
  //   0 128293 130313 6283b3 406383b3 7*7383b3 2383 2a383 128293 2a383 128293 2a383 128293 2a383 128293
  //   2a383 128293 2a383 62a023 128293 62a023 128293 62a023 128293
  //   CONTROL LOGIC
  //   USER INTERFACE
  //   RAM
endmodule

module IMEM (
  input  [31:0] ADDR,
  output [31:0] INST
);

  ROM #(.addrWidth(10), .dataWidth(32)) rom_1 (.addr(ADDR[9:0]), .data(INST));

  // Notes on the sheet:
  //   ROM
  //   contents of rom_1 (hex, n*v repeats v):
  //   0 128293 130313 6283b3 406383b3 7*7383b3 2383 2a383 128293 2a383 128293 2a383 128293 2a383 128293
  //   2a383 128293 2a383 62a023 128293 62a023 128293 62a023 128293
endmodule

module RegFile (
  input  [31:0] DataD,
  input  [4:0] AddrD,
  input  [4:0] AddrA,
  input  [4:0] AddrB,
  input  in_5,
  input  in_6,
  output [31:0] DataA,
  output [31:0] DataB
);

  wire WE_1, WE_2, WE_3, WE_4, WE_5, WE_6, WE_7, WE_8, WE_9, WE_10, WE_11, WE_12, WE_13, WE_14, WE_15, WE_16,
       WE_17, WE_18, WE_19, WE_20, WE_21, WE_22, WE_23, WE_24, WE_25, WE_26, WE_27, WE_28, WE_29, WE_30,
       WE_31;
  wire [31:0] in_r1, in_r2, in_r3, in_r4, in_r5, in_r6, in_r7, in_r8, in_r9, in_r10, in_r11, in_r12, in_r13,
       in_r14, in_r15, in_r16, in_r17, in_r18, in_r19, in_r20, in_r21, in_r22, in_r23, in_r24, in_r25,
       in_r26, in_r27, in_r28, in_r29, in_r30, in_r31, out_r1, out_r2, out_r3, out_r4, out_r5, out_r6,
       out_r7, out_r8, out_r9, out_r10, out_r11, out_r12, out_r13, out_r14, out_r15, out_r16, out_r17,
       out_r18, out_r19, out_r20, out_r21, out_r22, out_r23, out_r24, out_r25, out_r26, out_r27, out_r28,
       out_r29, out_r30, out_r31;

  Register #(.width(32)) register_1 (.D(in_r1), .en(WE_1), .clk(in_6), .Q(out_r1));  // open: clr
  Register #(.width(32)) register_2 (.D(in_r9), .en(WE_9), .clk(in_6), .Q(out_r9));  // open: clr
  Register #(.width(32)) register_3 (.D(in_r17), .en(WE_17), .clk(in_6), .Q(out_r17));  // open: clr
  Register #(.width(32)) register_4 (.D(in_r25), .en(WE_25), .clk(in_6), .Q(out_r25));  // open: clr
  Multiplexer #(.select(5), .width(32), .enable("false")) multiplexer_1 (
    .in0({32{1'b0}}), .in1(out_r1), .in2(out_r2), .in3(out_r3), .in4(out_r4), .in5(out_r5), .in6(out_r6),
    .in7(out_r7), .in8(out_r8), .in9(out_r9), .in10(out_r10), .in11(out_r11), .in12(out_r12), .in13(out_r13),
    .in14(out_r14), .in15(out_r15), .in16(out_r16), .in17(out_r17), .in18(out_r18), .in19(out_r19),
    .in20(out_r20), .in21(out_r21), .in22(out_r22), .in23(out_r23), .in24(out_r24), .in25(out_r25),
    .in26(out_r26), .in27(out_r27), .in28(out_r28), .in29(out_r29), .in30(out_r30), .in31(out_r31),
    .out(DataA), .sel(AddrA));
  Register #(.width(32)) register_5 (.D(in_r2), .en(WE_2), .clk(in_6), .Q(out_r2));  // open: clr
  Register #(.width(32)) register_6 (.D(in_r10), .en(WE_10), .clk(in_6), .Q(out_r10));  // open: clr
  Register #(.width(32)) register_7 (.D(in_r18), .en(WE_18), .clk(in_6), .Q(out_r18));  // open: clr
  Register #(.width(32)) register_8 (.D(in_r26), .en(WE_26), .clk(in_6), .Q(out_r26));  // open: clr
  Register #(.width(32)) register_9 (.D(in_r3), .en(WE_3), .clk(in_6), .Q(out_r3));  // open: clr
  Register #(.width(32)) register_10 (.D(in_r11), .en(WE_11), .clk(in_6), .Q(out_r11));  // open: clr
  Register #(.width(32)) register_11 (.D(in_r19), .en(WE_19), .clk(in_6), .Q(out_r19));  // open: clr
  Register #(.width(32)) register_12 (.D(in_r27), .en(WE_27), .clk(in_6), .Q(out_r27));  // open: clr
  Multiplexer #(.select(5), .width(32), .enable("false")) multiplexer_2 (
    .in0({32{1'b0}}), .in1(out_r1), .in2(out_r2), .in3(out_r3), .in4(out_r4), .in5(out_r5), .in6(out_r6),
    .in7(out_r7), .in8(out_r8), .in9(out_r9), .in10(out_r10), .in11(out_r11), .in12(out_r12), .in13(out_r13),
    .in14(out_r14), .in15(out_r15), .in16(out_r16), .in17(out_r17), .in18(out_r18), .in19(out_r19),
    .in20(out_r20), .in21(out_r21), .in22(out_r22), .in23(out_r23), .in24(out_r24), .in25(out_r25),
    .in26(out_r26), .in27(out_r27), .in28(out_r28), .in29(out_r29), .in30(out_r30), .in31(out_r31),
    .out(DataB), .sel(AddrB));
  Register #(.width(32)) register_13 (.D(in_r4), .en(WE_4), .clk(in_6), .Q(out_r4));  // open: clr
  Register #(.width(32)) register_14 (.D(in_r12), .en(WE_12), .clk(in_6), .Q(out_r12));  // open: clr
  Register #(.width(32)) register_15 (.D(in_r20), .en(WE_20), .clk(in_6), .Q(out_r20));  // open: clr
  Register #(.width(32)) register_16 (.D(in_r28), .en(WE_28), .clk(in_6), .Q(out_r28));  // open: clr
  Demultiplexer #(.select(5), .width(32)) demultiplexer_1 (
    .out1(in_r1), .out2(in_r2), .out3(in_r3), .out4(in_r4), .out5(in_r5), .out6(in_r6), .out7(in_r7),
    .out8(in_r8), .out9(in_r9), .out10(in_r10), .out11(in_r11), .out12(in_r12), .out13(in_r13),
    .out14(in_r14), .out15(in_r15), .out16(in_r16), .out17(in_r17), .out18(in_r18), .out19(in_r19),
    .out20(in_r20), .out21(in_r21), .out22(in_r22), .out23(in_r23), .out24(in_r24), .out25(in_r25),
    .out26(in_r26), .out27(in_r27), .out28(in_r28), .out29(in_r29), .out30(in_r30), .out31(in_r31),
    .in(DataD), .sel(AddrD), .en(in_5));  // open: out0
  Register #(.width(32)) register_17 (.D(in_r5), .en(WE_5), .clk(in_6), .Q(out_r5));  // open: clr
  Register #(.width(32)) register_18 (.D(in_r13), .en(WE_13), .clk(in_6), .Q(out_r13));  // open: clr
  Register #(.width(32)) register_19 (.D(in_r21), .en(WE_21), .clk(in_6), .Q(out_r21));  // open: clr
  Register #(.width(32)) register_20 (.D(in_r29), .en(WE_29), .clk(in_6), .Q(out_r29));  // open: clr
  Register #(.width(32)) register_21 (.D(in_r6), .en(WE_6), .clk(in_6), .Q(out_r6));  // open: clr
  Register #(.width(32)) register_22 (.D(in_r14), .en(WE_14), .clk(in_6), .Q(out_r14));  // open: clr
  Register #(.width(32)) register_23 (.D(in_r22), .en(WE_22), .clk(in_6), .Q(out_r22));  // open: clr
  Register #(.width(32)) register_24 (.D(in_r30), .en(WE_30), .clk(in_6), .Q(out_r30));  // open: clr
  Decoder #(.select(5)) decoder_1 (
    .out1(WE_1), .out2(WE_2), .out3(WE_3), .out4(WE_4), .out5(WE_5), .out6(WE_6), .out7(WE_7), .out8(WE_8),
    .out9(WE_9), .out10(WE_10), .out11(WE_11), .out12(WE_12), .out13(WE_13), .out14(WE_14), .out15(WE_15),
    .out16(WE_16), .out17(WE_17), .out18(WE_18), .out19(WE_19), .out20(WE_20), .out21(WE_21), .out22(WE_22),
    .out23(WE_23), .out24(WE_24), .out25(WE_25), .out26(WE_26), .out27(WE_27), .out28(WE_28), .out29(WE_29),
    .out30(WE_30), .out31(WE_31), .sel(AddrD), .en(in_5));  // open: out0
  Register #(.width(32)) register_25 (.D(in_r7), .en(WE_7), .clk(in_6), .Q(out_r7));  // open: clr
  Register #(.width(32)) register_26 (.D(in_r15), .en(WE_15), .clk(in_6), .Q(out_r15));  // open: clr
  Register #(.width(32)) register_27 (.D(in_r23), .en(WE_23), .clk(in_6), .Q(out_r23));  // open: clr
  Register #(.width(32)) register_28 (.D(in_r31), .en(WE_31), .clk(in_6), .Q(out_r31));  // open: clr
  Register #(.width(32)) register_29 (.D(in_r8), .en(WE_8), .clk(in_6), .Q(out_r8));  // open: clr
  Register #(.width(32)) register_30 (.D(in_r16), .en(WE_16), .clk(in_6), .Q(out_r16));  // open: clr
  Register #(.width(32)) register_31 (.D(in_r24), .en(WE_24), .clk(in_6), .Q(out_r24));  // open: clr

  // Other names for the same wires on the sheet: busA[31:0] = DataA; busB[31:0] = DataB; busW[31:0] = DataD;
  //   CLK = in_6; RA[4:0] = AddrA; RB[4:0] = AddrB; RW[4:0] = AddrD; WRITE_ENABLE = in_5

  // Notes on the sheet:
  //   Outputs
  //   I/O
  //   Inputs
  //   Register Reading
  //   Register Writing
  //   X0 HARDWIRED
endmodule

module ALU (
  input  [31:0] rs1,
  input  [31:0] rs2,
  input  [3:0] OP,
  output [31:0] R
);

  wire comparator_1_lt, comparator_2_lt;
  wire [31:0] o_add, o_and, o_or, o_sll, o_slt, o_sltu, o_sra, o_srl, o_sub, o_xor;

  Multiplexer #(.select(4), .width(32), .enable("false")) multiplexer_1 (
    .in0(o_add), .in1(o_sub), .in2(o_sll), .in3(o_slt), .in4(o_sltu), .in5(o_xor), .in6(o_srl), .in7(o_sra),
    .in8(o_or), .in9(o_and), .out(R), .sel(OP));  // open: in10, in11, in12, in13, in14, in15
  Adder #(.width(32)) adder_1 (.a(rs1), .b(rs2), .out(o_add));  // open: cin, cout
  Subtractor #(.width(32)) subtractor_1 (.a(rs1), .b(rs2), .out(o_sub));  // open: bin, bout
  Shifter #(.width(32)) shifter_1 (.in(rs1), .\dist (rs2[4:0]), .out(o_sll));
  Bit_Extender #(.in_width(1), .out_width(32)) bit_extender_1 (.out(o_slt));  // open: in
  Comparator #(.width(32)) comparator_1 (.a(rs1), .b(rs2), .lt(comparator_1_lt));  // open: gt, eq
  Bit_Extender #(.in_width(1), .out_width(32), .\type ("zero")) bit_extender_2 (.out(o_sltu));  // open: in
  Comparator #(.width(32)) comparator_2 (.a(rs1), .b(rs2), .lt(comparator_2_lt));  // open: gt, eq
  assign o_xor = rs1 ^ rs2;  // XOR_Gate xor_1, 32 bits wide
  Shifter #(.width(32), .shift("lr")) shifter_2 (.in(rs1), .\dist (rs2[4:0]), .out(o_srl));
  Shifter #(.width(32), .shift("ar")) shifter_3 (.in(rs1), .\dist (rs2[4:0]), .out(o_sra));
  assign o_or = rs1 | rs2;  // OR_Gate or_1, 32 bits wide
  assign o_and = rs1 & rs2;  // AND_Gate and_1, 32 bits wide

  // Other names for the same wires on the sheet: result[31:0] = R; X[31:0] = rs1; Y[31:0] = rs2

  // Notes on the sheet:
  //   Outputs
  //   I/O
  //   Operation Selection
  //   Inputs
  //   Operations
endmodule

module DMEM (
  input  [31:0] ADDR,
  input  MemRW,
  input  CLK,
  input  [31:0] DataW,
  output [31:0] DataR
);

  wire not_1_out;

  not not_1 (not_1_out, MemRW);
  RAM #(.addrWidth(10), .dataWidth(32), .databus("bibus")) ram_1 (
    .addr(ADDR[9:0]), .we(MemRW), .oe(not_1_out), .clk(CLK), .din(DataW), .dout(DataR));

  // Notes on the sheet:
  //   RAM
endmodule

module CONTROL_LOGIC (
  input  [31:0] Inst,
  output [6:0] out_2,
  output [4:0] out_3,
  output [2:0] out_4,
  output [4:0] out_5,
  output [4:0] out_6,
  output [6:0] out_7,
  output RegWEn,
  output BSel,
  output ImmSel,
  output [3:0] ALUSel,
  output WBSel,
  output MemRW
);

  wire comparator_5_eq, comparator_6_eq, comparator_7_eq, comparator_8_eq, comparator_9_eq, comparator_10_eq,
       comparator_11_eq, comparator_12_eq, comparator_13_eq, comparator_14_eq, comparator_15_eq,
       comparator_16_eq, comparator_17_eq, comparator_18_eq, comparator_19_eq, comparator_20_eq,
       comparator_21_eq, comparator_22_eq, comparator_23_eq, comparator_24_eq, comparator_25_eq,
       comparator_26_eq, comparator_27_eq, comparator_28_eq, comparator_29_eq, comparator_30_eq,
       comparator_31_eq, comparator_32_eq, comparator_33_eq, comparator_34_eq, comparator_35_eq,
       comparator_36_eq, comparator_37_eq, comparator_38_eq, comparator_39_eq, comparator_40_eq,
       comparator_41_eq, comparator_42_eq, comparator_43_eq, comparator_44_eq, comparator_45_eq,
       comparator_46_eq, comparator_47_eq, comparator_48_eq, comparator_49_eq, comparator_50_eq, I_add,
       I_and, I_lb, I_lbu, I_lh, I_lhu, I_lw, I_or, I_sll, I_slt, I_sltu, I_sra, I_srl, I_TYPE, I_TYPE_LOAD,
       I_xor, or_1_out, or_2_out, or_3_out, or_4_out, or_5_out, or_6_out, or_7_out, or_8_out, or_9_out,
       or_10_out, or_11_out, or_12_out, or_13_out, or_14_out, or_15_out, R_add, R_and, R_or, R_sll, R_slt,
       R_sltu, R_sra, R_srl, R_sub, R_TYPE, R_xor, S_sb, S_sh, S_sw, S_TYPE;

  or or_1 (or_1_out, R_add, S_TYPE, I_add);
  or or_2 (or_2_out, R_sll, I_sll);
  or or_3 (or_3_out, R_slt, I_slt);
  or or_4 (or_4_out, R_sltu, I_sltu);
  or or_5 (or_5_out, R_xor, I_xor);
  or or_6 (or_6_out, R_srl, I_srl);
  or or_7 (or_7_out, R_sra, I_sra);
  or or_8 (or_8_out, R_or, I_or);
  or or_9 (or_9_out, R_and, I_and);
  or or_10 (or_10_out, or_1_out, or_11_out);
  Comparator #(.width(7)) comparator_1 (.a(Inst[6:0]), .b(7'b0110011), .eq(R_TYPE));  // open: gt, lt
  Comparator #(.width(7)) comparator_2 (.a(Inst[6:0]), .b(7'b0010011), .eq(I_TYPE));  // open: gt, lt
  Comparator #(.width(7)) comparator_3 (.a(Inst[6:0]), .b(7'b0000011), .eq(I_TYPE_LOAD));  // open: gt, lt
  Comparator #(.width(7)) comparator_4 (.a(Inst[6:0]), .b(7'b0100011), .eq(S_TYPE));  // open: gt, lt
  buf or_11 (or_11_out, I_TYPE_LOAD);  // OR_Gate
  Priority_Encoder #(.select(4)) priority_encoder_1 (
    .in0(or_10_out), .in1(R_sub), .in2(or_2_out), .in3(or_3_out), .in4(or_4_out), .in5(or_5_out),
    .in6(or_6_out), .in7(or_7_out), .in8(or_8_out), .in9(or_9_out), .out(ALUSel));  // open: in10, in11, in12, in13, in14, in15, gs, en_out, en_in
  Comparator #(.width(3)) comparator_5 (.a(Inst[14:12]), .b(3'b000), .eq(comparator_5_eq));  // open: gt, lt
  Comparator #(.width(7)) comparator_6 (.a(Inst[31:25]), .b({7{1'b0}}), .eq(comparator_6_eq));  // open: gt, lt
  Comparator #(.width(3)) comparator_7 (.a(Inst[14:12]), .b(3'b000), .eq(comparator_7_eq));  // open: gt, lt
  Comparator #(.width(7)) comparator_8 (.a(Inst[31:25]), .b(7'b0100000), .eq(comparator_8_eq));  // open: gt, lt
  Comparator #(.width(3)) comparator_9 (.a(Inst[14:12]), .b(3'b001), .eq(comparator_9_eq));  // open: gt, lt
  Comparator #(.width(7)) comparator_10 (.a(Inst[31:25]), .b({7{1'b0}}), .eq(comparator_10_eq));  // open: gt, lt
  Comparator #(.width(3)) comparator_11 (.a(Inst[14:12]), .b(3'b010), .eq(comparator_11_eq));  // open: gt, lt
  Comparator #(.width(7)) comparator_12 (.a(Inst[31:25]), .b({7{1'b0}}), .eq(comparator_12_eq));  // open: gt, lt
  Comparator #(.width(3)) comparator_13 (.a(Inst[14:12]), .b(3'b011), .eq(comparator_13_eq));  // open: gt, lt
  Comparator #(.width(7)) comparator_14 (.a(Inst[31:25]), .b({7{1'b0}}), .eq(comparator_14_eq));  // open: gt, lt
  and and_1 (R_add, R_TYPE, comparator_5_eq, comparator_6_eq);
  and and_2 (R_sub, R_TYPE, comparator_7_eq, comparator_8_eq);
  and and_3 (R_sll, R_TYPE, comparator_9_eq, comparator_10_eq);
  and and_4 (R_slt, R_TYPE, comparator_11_eq, comparator_12_eq);
  and and_5 (R_sltu, R_TYPE, comparator_13_eq, comparator_14_eq);
  or or_12 (or_12_out, R_TYPE, I_TYPE_LOAD);
  or or_13 (or_13_out, I_TYPE, I_TYPE_LOAD, S_TYPE);
  or or_14 (or_14_out, I_TYPE, I_TYPE_LOAD);
  or or_15 (or_15_out, R_TYPE, I_TYPE);
  Priority_Encoder #(.select(1)) priority_encoder_2 (
    .in0(or_14_out), .in1(S_TYPE), .out(ImmSel));  // open: gs, en_out, en_in
  Priority_Encoder #(.select(1)) priority_encoder_3 (
    .in0(I_TYPE_LOAD), .in1(or_15_out), .out(WBSel));  // open: gs, en_out, en_in
  or or_16 (MemRW, S_sw, S_sh, S_sb);
  Comparator #(.width(3)) comparator_15 (.a(Inst[14:12]), .b(3'b100), .eq(comparator_15_eq));  // open: gt, lt
  Comparator #(.width(7)) comparator_16 (.a(Inst[31:25]), .b({7{1'b0}}), .eq(comparator_16_eq));  // open: gt, lt
  Comparator #(.width(3)) comparator_17 (.a(Inst[14:12]), .b(3'b101), .eq(comparator_17_eq));  // open: gt, lt
  Comparator #(.width(7)) comparator_18 (.a(Inst[31:25]), .b({7{1'b0}}), .eq(comparator_18_eq));  // open: gt, lt
  Comparator #(.width(3)) comparator_19 (.a(Inst[14:12]), .b(3'b101), .eq(comparator_19_eq));  // open: gt, lt
  Comparator #(.width(7)) comparator_20 (.a(Inst[31:25]), .b(7'b0100000), .eq(comparator_20_eq));  // open: gt, lt
  Comparator #(.width(3)) comparator_21 (.a(Inst[14:12]), .b(3'b110), .eq(comparator_21_eq));  // open: gt, lt
  Comparator #(.width(7)) comparator_22 (.a(Inst[31:25]), .b({7{1'b0}}), .eq(comparator_22_eq));  // open: gt, lt
  Comparator #(.width(3)) comparator_23 (.a(Inst[14:12]), .b(3'b111), .eq(comparator_23_eq));  // open: gt, lt
  Comparator #(.width(7)) comparator_24 (.a(Inst[31:25]), .b({7{1'b0}}), .eq(comparator_24_eq));  // open: gt, lt
  or or_17 (RegWEn, or_12_out, I_TYPE);
  Priority_Encoder #(.select(1)) priority_encoder_4 (
    .in0(R_TYPE), .in1(or_13_out), .out(BSel));  // open: gs, en_out, en_in
  and and_6 (R_xor, R_TYPE, comparator_15_eq, comparator_16_eq);
  and and_7 (R_srl, R_TYPE, comparator_17_eq, comparator_18_eq);
  and and_8 (R_sra, R_TYPE, comparator_19_eq, comparator_20_eq);
  and and_9 (R_or, R_TYPE, comparator_21_eq, comparator_22_eq);
  and and_10 (R_and, R_TYPE, comparator_23_eq, comparator_24_eq);
  Comparator #(.width(3)) comparator_25 (.a(Inst[14:12]), .b(3'b000), .eq(comparator_25_eq));  // open: gt, lt
  Comparator #(.width(7)) comparator_26 (.a(Inst[31:25]), .b({7{1'b0}}), .eq(comparator_26_eq));  // open: gt, lt
  Comparator #(.width(3)) comparator_27 (.a(Inst[14:12]), .b(3'b001), .eq(comparator_27_eq));  // open: gt, lt
  Comparator #(.width(7)) comparator_28 (.a(Inst[31:25]), .b({7{1'b0}}), .eq(comparator_28_eq));  // open: gt, lt
  Comparator #(.width(3)) comparator_29 (.a(Inst[14:12]), .b(3'b010), .eq(comparator_29_eq));  // open: gt, lt
  Comparator #(.width(7)) comparator_30 (.a(Inst[31:25]), .b({7{1'b0}}), .eq(comparator_30_eq));  // open: gt, lt
  Comparator #(.width(3)) comparator_31 (.a(Inst[14:12]), .b(3'b011), .eq(comparator_31_eq));  // open: gt, lt
  Comparator #(.width(7)) comparator_32 (.a(Inst[31:25]), .b({7{1'b0}}), .eq(comparator_32_eq));  // open: gt, lt
  Comparator #(.width(3)) comparator_33 (.a(Inst[14:12]), .b(3'b100), .eq(comparator_33_eq));  // open: gt, lt
  Comparator #(.width(7)) comparator_34 (.a(Inst[31:25]), .b({7{1'b0}}), .eq(comparator_34_eq));  // open: gt, lt
  and and_11 (I_add, I_TYPE, comparator_25_eq, comparator_26_eq);
  and and_12 (I_sll, I_TYPE, comparator_27_eq, comparator_28_eq);
  and and_13 (I_slt, I_TYPE, comparator_29_eq, comparator_30_eq);
  and and_14 (I_sltu, I_TYPE, comparator_31_eq, comparator_32_eq);
  and and_15 (I_xor, I_TYPE, comparator_33_eq, comparator_34_eq);
  Comparator #(.width(3)) comparator_35 (.a(Inst[14:12]), .b(3'b101), .eq(comparator_35_eq));  // open: gt, lt
  Comparator #(.width(7)) comparator_36 (.a(Inst[31:25]), .b({7{1'b0}}), .eq(comparator_36_eq));  // open: gt, lt
  Comparator #(.width(3)) comparator_37 (.a(Inst[14:12]), .b(3'b101), .eq(comparator_37_eq));  // open: gt, lt
  Comparator #(.width(7)) comparator_38 (.a(Inst[31:25]), .b(7'b0100000), .eq(comparator_38_eq));  // open: gt, lt
  Comparator #(.width(3)) comparator_39 (.a(Inst[14:12]), .b(3'b110), .eq(comparator_39_eq));  // open: gt, lt
  Comparator #(.width(7)) comparator_40 (.a(Inst[31:25]), .b({7{1'b0}}), .eq(comparator_40_eq));  // open: gt, lt
  Comparator #(.width(3)) comparator_41 (.a(Inst[14:12]), .b(3'b111), .eq(comparator_41_eq));  // open: gt, lt
  Comparator #(.width(7)) comparator_42 (.a(Inst[31:25]), .b({7{1'b0}}), .eq(comparator_42_eq));  // open: gt, lt
  and and_16 (I_srl, I_TYPE, comparator_35_eq, comparator_36_eq);
  and and_17 (I_sra, I_TYPE, comparator_37_eq, comparator_38_eq);
  and and_18 (I_or, I_TYPE, comparator_39_eq, comparator_40_eq);
  and and_19 (I_and, I_TYPE, comparator_41_eq, comparator_42_eq);
  Comparator #(.width(3)) comparator_43 (.a(Inst[14:12]), .b(3'b000), .eq(comparator_43_eq));  // open: gt, lt
  Comparator #(.width(3)) comparator_44 (.a(Inst[14:12]), .b(3'b001), .eq(comparator_44_eq));  // open: gt, lt
  Comparator #(.width(3)) comparator_45 (.a(Inst[14:12]), .b(3'b010), .eq(comparator_45_eq));  // open: gt, lt
  Comparator #(.width(3)) comparator_46 (.a(Inst[14:12]), .b(3'b100), .eq(comparator_46_eq));  // open: gt, lt
  Comparator #(.width(3)) comparator_47 (.a(Inst[14:12]), .b(3'b101), .eq(comparator_47_eq));  // open: gt, lt
  and and_20 (I_lb, I_TYPE_LOAD, comparator_43_eq);
  and and_21 (I_lh, I_TYPE_LOAD, comparator_44_eq);
  and and_22 (I_lw, I_TYPE_LOAD, comparator_45_eq);
  and and_23 (I_lbu, I_TYPE_LOAD, comparator_46_eq);
  and and_24 (I_lhu, I_TYPE_LOAD, comparator_47_eq);
  Comparator #(.width(3)) comparator_48 (.a(Inst[14:12]), .b(3'b010), .eq(comparator_48_eq));  // open: gt, lt
  Comparator #(.width(3)) comparator_49 (.a(Inst[14:12]), .b(3'b001), .eq(comparator_49_eq));  // open: gt, lt
  Comparator #(.width(3)) comparator_50 (.a(Inst[14:12]), .b(3'b000), .eq(comparator_50_eq));  // open: gt, lt
  and and_25 (S_sw, S_TYPE, comparator_48_eq);
  and and_26 (S_sh, S_TYPE, comparator_49_eq);
  and and_27 (S_sb, S_TYPE, comparator_50_eq);

  assign out_2 = Inst[6:0];
  assign out_3 = Inst[11:7];
  assign out_4 = Inst[14:12];
  assign out_5 = Inst[19:15];
  assign out_6 = Inst[24:20];
  assign out_7 = Inst[31:25];

  // Other names for the same wires on the sheet: ALU_OP[3:0] = ALUSel; OPCODE[6:0] = Inst[6:0];
  //   IMM_4_0[4:0] = Inst[11:7]; RD[4:0] = Inst[11:7]; FUNCT3[2:0] = Inst[14:12]; RS1[4:0] = Inst[19:15];
  //   IMM_11_0[11:0] = Inst[31:20]; RS2[4:0] = Inst[24:20]; FUNCT7[6:0] = Inst[31:25]; IMM_11_5[6:0] = Inst[31:25]

  // Notes on the sheet:
  //   EXECUTE
  //   ALU Operation Encoding
  //   INSTRUCTION DECODING
  //   R-TYPE
  //   I-TYPE
  //   WRITE BACK
  //   S-Type
  //   Memory Write Selection
endmodule

module Imm_Gen (
  input  [31:0] Inst,
  input  ImmSel,
  output [31:0] Imm
);

  Multiplexer #(.width(32), .enable("false")) multiplexer_1 (
    .in0({{21{Inst[31]}}, Inst[30:20]}), .in1({{21{Inst[31]}}, Inst[30:25], Inst[11:7]}), .out(Imm),
    .sel(ImmSel));

  // Other names for the same wires on the sheet: FUNCT3[2:0] = Inst[14:12]; FUNCT7[6:0] = Inst[31:25];
  //   I_TYPE[31:0] = {{21{Inst[31]}}, Inst[30:20]}; S_TYPE[31:0] = {{21{Inst[31]}}, Inst[30:25], Inst[11:7]};
  //   OPCODE[6:0] = Inst[6:0]; RD[4:0] = Inst[11:7]; RS1[4:0] = Inst[19:15]; RS2[4:0] = Inst[24:20]
endmodule
